// Logisim project ULA (C1) - Somador 8 Bits.circ as structural Verilog
module Somador_de_4_bits (
  input  a2,
  input  a0,
  input  b2,
  input  b0,
  input  cin,
  input  a3,
  input  a1,
  input  b3,
  input  b1,
  output s3,
  output s1,
  output s4,
  output s2,
  output cout
);

  wire and_1_out, and_2_out, and_3_out, and_4_out, and_5_out, and_6_out, and_7_out, and_8_out, and_9_out,
       and_10_out, and_11_out, and_12_out, or_1_out, or_2_out, or_3_out, xor_1_out, xor_2_out, xor_5_out,
       xor_6_out;

  and and_1 (and_1_out, a0, b0);
  and and_2 (and_2_out, a0, cin);
  and and_3 (and_3_out, b0, cin);
  and and_4 (and_4_out, a1, b1);
  and and_5 (and_5_out, a1, or_1_out);
  and and_6 (and_6_out, b1, or_1_out);
  xor xor_1 (xor_1_out, a0, b0);
  xor xor_2 (xor_2_out, a1, b1);
  xor xor_3 (s1, xor_1_out, cin);
  or or_1 (or_1_out, and_1_out, and_2_out, and_3_out);
  xor xor_4 (s2, xor_2_out, or_1_out);
  or or_2 (or_2_out, and_4_out, and_5_out, and_6_out);
  xor xor_5 (xor_5_out, a2, b2);
  and and_7 (and_7_out, a2, b2);
  and and_8 (and_8_out, a2, or_2_out);
  and and_9 (and_9_out, b2, or_2_out);
  xor xor_6 (xor_6_out, a3, b3);
  and and_10 (and_10_out, a3, b3);
  and and_11 (and_11_out, a3, or_3_out);
  and and_12 (and_12_out, b3, or_3_out);
  xor xor_7 (s3, xor_5_out, or_2_out);
  or or_3 (or_3_out, and_7_out, and_8_out, and_9_out);
  xor xor_8 (s4, xor_6_out, or_3_out);
  or or_4 (cout, and_10_out, and_11_out, and_12_out);

  // Notes on the sheet:
  //   cin
  //   cin
  //   cin
endmodule

module Somador_de_8_Bits (
  input  in_1,
  input  in_2,
  input  in_3,
  input  in_4,
  input  in_5,
  input  in_6,
  input  in_7,
  input  in_8,
  input  in_9,
  input  in_10,
  input  in_11,
  input  in_12,
  input  in_13,
  input  in_14,
  input  in_15,
  input  in_16,
  output out_17,
  output out_18,
  output out_19,
  output out_20,
  output out_21,
  output out_22,
  output out_23,
  output out_24,
  output out_25
);

  wire somador_de_4_bits_1_cout;

  Somador_de_4_bits somador_de_4_bits_1 (
    .a2(in_3), .a0(in_1), .b2(in_11), .b0(in_9), .cin(1'b0), .a3(in_4), .a1(in_2), .b3(in_12), .b1(in_10),
    .s3(out_18), .s1(out_20), .s4(out_17), .s2(out_19), .cout(somador_de_4_bits_1_cout));
  Somador_de_4_bits somador_de_4_bits_2 (
    .a2(in_7), .a0(in_5), .b2(in_15), .b0(in_13), .cin(somador_de_4_bits_1_cout), .a3(in_8), .a1(in_6),
    .b3(in_16), .b1(in_14), .s3(out_23), .s1(out_25), .s4(out_22), .s2(out_24), .cout(out_21));

  // Other names for the same wires on the sheet: a0 = in_1; a1 = in_2; a2 = in_3; a3 = in_4; a4 = in_5; a5 = in_6;
  //   a6 = in_7; a7 = in_8; b0 = in_9; b1 = in_10; b2 = in_11; b3 = in_12; b4 = in_13; b5 = in_14; b6 = in_15;
  //   b7 = in_16

  // Notes on the sheet:
  //   Entrada A de 4 Bits
  //   Entrada B de 4 Bits
endmodule
