// Logisim project ULA (C1) - Sub 8 Bits.circ as structural Verilog
module Somador_de_4_bits (
  input  a2,
  input  a0,
  input  b2,
  input  b0,
  input  cin,
  input  a3,
  input  a1,
  input  b3,
  input  b1,
  output s3,
  output s1,
  output s4,
  output s2,
  output cout
);

  wire and_1_out, and_2_out, and_3_out, and_4_out, and_5_out, and_6_out, and_7_out, and_8_out, and_9_out,
       and_10_out, and_11_out, and_12_out, or_1_out, or_2_out, or_3_out, xor_1_out, xor_2_out, xor_5_out,
       xor_6_out;

  and and_1 (and_1_out, a0, b0);
  and and_2 (and_2_out, a0, cin);
  and and_3 (and_3_out, b0, cin);
  and and_4 (and_4_out, a1, b1);
  and and_5 (and_5_out, a1, or_1_out);
  and and_6 (and_6_out, b1, or_1_out);
  xor xor_1 (xor_1_out, a0, b0);
  xor xor_2 (xor_2_out, a1, b1);
  xor xor_3 (s1, xor_1_out, cin);
  or or_1 (or_1_out, and_1_out, and_2_out, and_3_out);
  xor xor_4 (s2, xor_2_out, or_1_out);
  or or_2 (or_2_out, and_4_out, and_5_out, and_6_out);
  xor xor_5 (xor_5_out, a2, b2);
  and and_7 (and_7_out, a2, b2);
  and and_8 (and_8_out, a2, or_2_out);
  and and_9 (and_9_out, b2, or_2_out);
  xor xor_6 (xor_6_out, a3, b3);
  and and_10 (and_10_out, a3, b3);
  and and_11 (and_11_out, a3, or_3_out);
  and and_12 (and_12_out, b3, or_3_out);
  xor xor_7 (s3, xor_5_out, or_2_out);
  or or_3 (or_3_out, and_7_out, and_8_out, and_9_out);
  xor xor_8 (s4, xor_6_out, or_3_out);
  or or_4 (cout, and_10_out, and_11_out, and_12_out);

  // Notes on the sheet:
  //   cin
  //   cin
  //   cin
endmodule

module Somador_de_8_Bits (
  input  a0,
  input  b0,
  input  a1,
  input  b1,
  input  a2,
  input  b2,
  input  a3,
  input  b3,
  input  cin,
  input  a4,
  input  b4,
  input  a5,
  input  b5,
  input  a6,
  input  b6,
  input  a7,
  input  b7,
  output out_18,
  output out_19,
  output out_20,
  output out_21,
  output out_22,
  output out_23,
  output out_24,
  output out_25,
  output out_26
);

  wire somador_de_4_bits_2_cout;

  Somador_de_4_bits somador_de_4_bits_1 (
    .a2(a6), .a0(a4), .b2(b6), .b0(b4), .cin(somador_de_4_bits_2_cout), .a3(a7), .a1(a5), .b3(b7), .b1(b5),
    .s3(out_24), .s1(out_26), .s4(out_23), .s2(out_25), .cout(out_22));
  Somador_de_4_bits somador_de_4_bits_2 (
    .a2(a2), .a0(a0), .b2(b2), .b0(b0), .cin(cin), .a3(a3), .a1(a1), .b3(b3), .b1(b1), .s3(out_19),
    .s1(out_21), .s4(out_18), .s2(out_20), .cout(somador_de_4_bits_2_cout));

  // Notes on the sheet:
  //   cin
endmodule

module subtrator__bits (
  input  a0,
  input  b0,
  input  a1,
  input  b1,
  input  a2,
  input  b2,
  input  a3,
  input  b3,
  input  a4,
  input  b4,
  input  a5,
  input  b5,
  input  a6,
  input  b6,
  input  a7,
  input  b7
);

  wire d0, d1, d2, d3, d4, d5, d6, d7, not_1_out, not_2_out, not_3_out, not_4_out, not_5_out, not_6_out,
       not_7_out, not_8_out;

  not not_1 (not_1_out, b0);
  Somador_de_8_Bits somador_de_8_bits_1 (
    .a0(a0), .b0(not_1_out), .a1(a1), .b1(not_2_out), .a2(a2), .b2(not_3_out), .a3(a3), .b3(not_4_out),
    .a4(a4), .b4(not_5_out), .a5(a5), .b5(not_6_out), .a6(a6), .b6(not_7_out), .a7(a7), .b7(not_8_out),
    .out_23(d7), .out_24(d6), .out_25(d5), .out_26(d4), .out_18(d3), .out_19(d2), .out_20(d1), .out_21(d0),
    .cin(1'b1));  // open: out_22
  not not_2 (not_2_out, b1);
  not not_3 (not_3_out, b2);
  not not_4 (not_4_out, b3);
  not not_5 (not_5_out, b4);
  not not_6 (not_6_out, b5);
  not not_7 (not_7_out, b6);
  not not_8 (not_8_out, b7);
endmodule
