// Logisim project ULA (C11) - Espelhador de 8 Bits.circ as structural Verilog
module EspelharBits (
  input  a0,
  input  a1,
  input  a2,
  input  a3,
  input  a4,
  input  a5,
  input  a6,
  input  a7,
  output a0_2,
  output a1_2,
  output a2_2,
  output a3_2,
  output a4_2,
  output a5_2,
  output a6_2,
  output a7_2
);


  assign a0_2 = a7;
  assign a1_2 = a6;
  assign a2_2 = a5;
  assign a3_2 = a4;
  assign a4_2 = a3;
  assign a5_2 = a2;
  assign a6_2 = a1;
  assign a7_2 = a0;
endmodule

module Espelhar8Bits (
  input  in_1,
  input  in_2,
  input  in_3,
  input  in_4,
  input  in_5,
  input  in_6,
  input  in_7,
  input  in_8,
  output out_9,
  output out_10,
  output out_11,
  output out_12,
  output out_13,
  output out_14,
  output out_15,
  output out_16
);

  EspelharBits espelharbits_1 (
    .a0(in_1), .a1(in_2), .a2(in_3), .a3(in_4), .a4(in_5), .a5(in_6), .a6(in_7), .a7(in_8), .a0_2(out_9),
    .a1_2(out_10), .a2_2(out_11), .a3_2(out_12), .a4_2(out_13), .a5_2(out_14), .a6_2(out_15), .a7_2(out_16));

  // Other names for the same wires on the sheet: a0 = in_1; a1 = in_2; a2 = in_3; a3 = in_4; a4 = in_5; a5 = in_6;
  //   a6 = in_7; a7 = in_8
endmodule
