// Logisim project ULA (C13) - OR.circ as structural Verilog
module OR (
  input  in_1,
  input  in_2,
  input  in_3,
  input  in_4,
  input  in_5,
  input  in_6,
  input  in_7,
  input  in_8,
  input  in_9,
  input  in_10,
  input  in_11,
  input  in_12,
  input  in_13,
  input  in_14,
  input  in_15,
  input  in_16,
  output s0,
  output s4,
  output s1,
  output s5,
  output s2,
  output s7,
  output s3,
  output s8
);

  or or_1 (s0, in_1, in_9);
  or or_2 (s1, in_2, in_10);
  or or_3 (s2, in_3, in_11);
  or or_4 (s3, in_4, in_12);
  or or_5 (s4, in_5, in_13);
  or or_6 (s5, in_6, in_14);
  or or_7 (s7, in_7, in_15);
  or or_8 (s8, in_8, in_16);

  // Other names for the same wires on the sheet: a0 = in_1; a1 = in_2; a2 = in_3; a3 = in_4; a4 = in_5; a5 = in_6;
  //   a6 = in_7; a7 = in_8; b0 = in_9; b1 = in_10; b2 = in_11; b3 = in_12; b4 = in_13; b5 = in_14; b6 = in_15;
  //   b7 = in_16

  // Notes on the sheet:
  //   Entrada A de 8 Bits
  //   Entrada B de 8 Bits
  //   Circuito OR de 8 Bits
endmodule

module OR_8_BITS (
  input  in_1,
  input  in_2,
  input  in_3,
  input  in_4,
  input  in_5,
  input  in_6,
  input  in_7,
  input  in_8,
  input  in_9,
  input  in_10,
  input  in_11,
  input  in_12,
  input  in_13,
  input  in_14,
  input  in_15,
  input  in_16,
  output out_17,
  output out_18,
  output out_19,
  output out_20,
  output out_21,
  output out_22,
  output out_23,
  output out_24
);

  OR or_1 (
    .in_1(in_1), .in_2(in_2), .in_3(in_3), .in_4(in_4), .in_5(in_5), .in_6(in_6), .in_7(in_7), .in_8(in_8),
    .in_9(in_9), .in_10(in_10), .in_11(in_11), .in_12(in_12), .in_13(in_13), .in_14(in_14), .in_15(in_15),
    .in_16(in_16), .s0(out_17), .s1(out_18), .s2(out_19), .s3(out_20), .s4(out_21), .s5(out_22), .s7(out_23),
    .s8(out_24));

  // Other names for the same wires on the sheet: a0 = in_1; a1 = in_2; a2 = in_3; a3 = in_4; a4 = in_5; a5 = in_6;
  //   a6 = in_7; a7 = in_8; b0 = in_9; b1 = in_10; b2 = in_11; b3 = in_12; b4 = in_13; b5 = in_14; b6 = in_15;
  //   b7 = in_16

  // Notes on the sheet:
  //   Entrada A de 8 Bits
  //   Entrada B de 8 Bits
  //   Circuito OR de 8 Bits
endmodule
