// Logisim project ULA (C4) - Incrementador 8 Bits.circ as structural Verilog
module Incrementador_8_Bits (
  input  in_1,
  input  in_2,
  input  in_3,
  input  in_4,
  input  in_5,
  input  in_6,
  input  in_7,
  input  in_8,
  output s2,
  output s0,
  output s3,
  output s1,
  output s4,
  output s6,
  output s7,
  output s5,
  output cout
);

  wire and_1_out, and_2_out, and_3_out, and_4_out, and_5_out, and_6_out, and_7_out, and_8_out, and_9_out,
       and_10_out, and_11_out, and_12_out, and_13_out, and_14_out, and_15_out, and_16_out, and_17_out,
       and_18_out, and_19_out, and_20_out, and_21_out, and_22_out, and_23_out, and_24_out, or_1_out,
       or_2_out, or_3_out, or_4_out, or_5_out, or_6_out, or_7_out, xor_1_out, xor_2_out, xor_3_out,
       xor_4_out, xor_9_out, xor_10_out, xor_11_out, xor_12_out;

  xor xor_1 (xor_1_out, in_1, 1'b1);
  and and_1 (and_1_out, in_1, 1'b1);
  and and_2 (and_2_out, in_1, 1'b0);
  and and_3 (and_3_out, 1'b1, 1'b0);
  xor xor_2 (xor_2_out, in_2, 1'b0);
  and and_4 (and_4_out, in_2, 1'b0);
  and and_5 (and_5_out, in_2, or_3_out);
  and and_6 (and_6_out, 1'b0, or_3_out);
  xor xor_3 (xor_3_out, in_5, 1'b0);
  and and_7 (and_7_out, in_5, 1'b0);
  and and_8 (and_8_out, in_5, or_6_out);
  and and_9 (and_9_out, 1'b0, or_6_out);
  xor xor_4 (xor_4_out, in_6, 1'b0);
  and and_10 (and_10_out, in_6, 1'b0);
  and and_11 (and_11_out, in_6, or_1_out);
  and and_12 (and_12_out, 1'b0, or_1_out);
  xor xor_5 (s4, xor_3_out, or_6_out);
  or or_1 (or_1_out, and_7_out, and_8_out, and_9_out);
  xor xor_6 (s5, xor_4_out, or_1_out);
  or or_2 (or_2_out, and_10_out, and_11_out, and_12_out);
  xor xor_7 (s0, xor_1_out, 1'b0);
  or or_3 (or_3_out, and_1_out, and_2_out, and_3_out);
  xor xor_8 (s1, xor_2_out, or_3_out);
  or or_4 (or_4_out, and_4_out, and_5_out, and_6_out);
  xor xor_9 (xor_9_out, in_3, 1'b0);
  and and_13 (and_13_out, in_3, 1'b0);
  and and_14 (and_14_out, in_3, or_4_out);
  and and_15 (and_15_out, 1'b0, or_4_out);
  xor xor_10 (xor_10_out, in_4, 1'b0);
  and and_16 (and_16_out, in_4, 1'b0);
  and and_17 (and_17_out, in_4, or_5_out);
  and and_18 (and_18_out, 1'b0, or_5_out);
  xor xor_11 (xor_11_out, in_7, 1'b0);
  and and_19 (and_19_out, in_7, 1'b0);
  and and_20 (and_20_out, in_7, or_2_out);
  and and_21 (and_21_out, 1'b0, or_2_out);
  xor xor_12 (xor_12_out, in_8, 1'b0);
  and and_22 (and_22_out, in_8, 1'b0);
  and and_23 (and_23_out, in_8, or_7_out);
  and and_24 (and_24_out, 1'b0, or_7_out);
  xor xor_13 (s2, xor_9_out, or_4_out);
  or or_5 (or_5_out, and_13_out, and_14_out, and_15_out);
  xor xor_14 (s3, xor_10_out, or_5_out);
  or or_6 (or_6_out, and_16_out, and_17_out, and_18_out);
  xor xor_15 (s6, xor_11_out, or_2_out);
  or or_7 (or_7_out, and_19_out, and_20_out, and_21_out);
  xor xor_16 (s7, xor_12_out, or_7_out);
  or or_8 (cout, and_22_out, and_23_out, and_24_out);

  // Other names for the same wires on the sheet: a0 = in_1; a1 = in_2; a2 = in_3; a3 = in_4; a4 = in_5; a5 = in_6;
  //   a6 = in_7; a7 = in_8

  // Notes on the sheet:
  //   Entrada A de 8 Bits
  //   Entrada B de 8 Bits
  //   Circuito Incrementador
  //   cin
  //   cin
  //   cin
  //   cin
  //   cin
  //   cin
  //   cin
endmodule

module Incrementador_de_8_Bits (
  input  in_1,
  input  in_2,
  input  in_3,
  input  in_4,
  input  in_5,
  input  in_6,
  input  in_7,
  input  in_8,
  output s0,
  output s1,
  output s2,
  output s3,
  output s4,
  output s5,
  output s6,
  output s7,
  output cout
);

  Incrementador_8_Bits incrementador_8_bits_1 (
    .in_1(in_1), .in_2(in_2), .in_3(in_3), .in_4(in_4), .in_5(in_5), .in_6(in_6), .in_7(in_7), .in_8(in_8),
    .s2(s2), .s0(s0), .s3(s3), .s1(s1), .s4(s4), .s6(s6), .s7(s7), .s5(s5), .cout(cout));

  // Other names for the same wires on the sheet: a0 = in_1; a1 = in_2; a2 = in_3; a3 = in_4; a4 = in_5; a5 = in_6;
  //   a6 = in_7; a7 = in_8

  // Notes on the sheet:
  //   Circuito Incrementador
  //   Entrada A de 8 Bits
  //   Entrada B de 8 Bits (1 bit 1 e 7 bits 0)
endmodule
