// Logisim project cir_10.circ as structural Verilog: 1 circuit, main circuit main
module main (
  input  a0,
  input  a1,
  input  a2,
  input  a3,
  input  a4,
  input  a5,
  input  a6,
  input  a7,
  output s0,
  output s1,
  output s2,
  output s3,
  output s4,
  output s5,
  output s6,
  output s7
);


  assign s0 = a4;
  assign s1 = a5;
  assign s2 = a6;
  assign s3 = a7;
  assign s4 = a0;
  assign s5 = a1;
  assign s6 = a2;
  assign s7 = a3;

  // Other names for the same wires on the sheet: a0_14 = a0; a1_14 = a1; a2_14 = a2; a3_14 = a3; a4_14 = a4;
  //   a5_14 = a5; a6_14 = a6; a7_14 = a7

  // Notes on the sheet:
  //   A - 8 bits
endmodule
