// Logisim project cir_12.circ as structural Verilog: 1 circuit, main circuit main
module main (
  input  A___8_bits,
  input  in_2,
  input  in_3,
  input  in_4,
  input  in_5,
  input  in_6,
  input  in_7,
  input  in_8,
  input  in_9,
  input  in_10,
  input  in_11,
  input  in_12,
  input  in_13,
  input  in_14,
  input  in_15,
  input  in_16,
  output s0,
  output s4,
  output s1,
  output s5,
  output s2,
  output s6,
  output s3,
  output s7
);

  and and_1 (s0, A___8_bits, in_2);
  and and_2 (s1, in_3, in_4);
  and and_3 (s2, in_5, in_6);
  and and_4 (s3, in_7, in_8);
  and and_5 (s4, in_9, in_10);
  and and_6 (s5, in_11, in_12);
  and and_7 (s6, in_13, in_14);
  and and_8 (s7, in_15, in_16);

  // Other names for the same wires on the sheet: a0_14 = A___8_bits; a1_14 = in_3; a2_14 = in_5; a3_14 = in_7;
  //   a4_14 = in_9; a5_14 = in_11; a6_14 = in_13; a7_14 = in_15; b0_14 = in_2; b1_14 = in_4; b2_14 = in_6;
  //   b3_14 = in_8; b4_14 = in_10; b5_14 = in_12; b6_14 = in_14; b7_14 = in_16

  // Notes on the sheet:
  //   B - 8 bits
endmodule
