// Logisim project cir_14.circ as structural Verilog: 1 circuit, main circuit main
module main (
  input  a0,
  input  b0,
  input  a1,
  input  b1,
  input  a2,
  input  b2,
  input  a3,
  input  b3,
  input  a4,
  input  b4,
  input  a5,
  input  b5,
  input  a6,
  input  b6,
  input  a7,
  input  b7,
  output s0,
  output s4,
  output s1,
  output s5,
  output s2,
  output s6,
  output s3,
  output s7
);

  xor xor_1 (s0, a0, b0);
  xor xor_2 (s1, a1, b1);
  xor xor_3 (s2, a2, b2);
  xor xor_4 (s3, a3, b3);
  xor xor_5 (s4, a4, b4);
  xor xor_6 (s5, a5, b5);
  xor xor_7 (s6, a6, b6);
  xor xor_8 (s7, a7, b7);

  // Other names for the same wires on the sheet: a0_14 = a0; a1_14 = a1; a2_14 = a2; a3_14 = a3; a4_14 = a4;
  //   a5_14 = a5; a6_14 = a6; a7_14 = a7; b0_14 = b0; b1_14 = b1; b2_14 = b2; b3_14 = b3; b4_14 = b4; b5_14 = b5;
  //   b6_14 = b6; b7_14 = b7

  // Notes on the sheet:
  //   A - 8 bits
  //   B - 8 bits
endmodule
