// Logisim project cir_15.circ as structural Verilog: 1 circuit, main circuit main
module main (
  input  a0,
  input  a1,
  input  a2,
  input  a3,
  input  a4,
  input  a5,
  input  a6,
  input  a7,
  output s0,
  output s1,
  output s2,
  output s3,
  output s4,
  output s5,
  output s6,
  output s7
);

  not not_1 (s0, a0);
  not not_2 (s1, a1);
  not not_3 (s2, a2);
  not not_4 (s3, a3);
  not not_5 (s4, a4);
  not not_6 (s5, a5);
  not not_7 (s6, a6);
  not not_8 (s7, a7);

  // Notes on the sheet:
  //   A - 8 bits
endmodule
