// Logisim project cir_5.circ as structural Verilog: 3 circuits, main circuit main
module main (
  input  a0,
  input  a1,
  input  a2,
  input  a3,
  input  a4,
  input  a5,
  input  a6,
  input  a7,
  output s0,
  output s1,
  output s2,
  output s3,
  output s4,
  output s5,
  output s6,
  output s7,
  output c_out
);

  eight_bit_calculator eight_bit_calculator_1 (
    .a0(a0), .a1(a1), .a2(a2), .a3(a3), .c_in(1'b0), .a4(a4), .a5(a5), .a6(a6), .a7(a7), .b0(1'b1),
    .b1(1'b1), .b2(1'b1), .b3(1'b1), .b4(1'b1), .b5(1'b1), .b6(1'b1), .b7(1'b1), .s0(s0), .s1(s1), .s2(s2),
    .s3(s3), .s4(s4), .s5(s5), .s6(s6), .s7(s7), .c_out(c_out));

  // Notes on the sheet:
  //   A - 8 bits
  //   -1 - 8 bits
endmodule

module two_bit_adder (
  input  A,
  input  B,
  input  c_in,
  output S,
  output c_out
);

  wire and_1_out, and_2_out, xor_1_out;

  xor xor_1 (xor_1_out, A, B);
  and and_1 (and_1_out, A, B);
  xor xor_2 (S, xor_1_out, c_in);
  and and_2 (and_2_out, c_in, xor_1_out);
  or or_1 (c_out, and_2_out, and_1_out);
endmodule

module eight_bit_calculator (
  input  a0,
  input  a1,
  input  a2,
  input  a3,
  input  c_in,
  input  a4,
  input  a5,
  input  a6,
  input  a7,
  input  b0,
  input  b1,
  input  b2,
  input  b3,
  input  b4,
  input  b5,
  input  b6,
  input  b7,
  output s0,
  output s1,
  output s2,
  output s3,
  output s4,
  output s5,
  output s6,
  output s7,
  output c_out
);

  wire c0, c1, c2, c3, c4, c5, c6;

  two_bit_adder two_bit_adder_1 (.A(a0), .B(b0), .c_in(c_in), .S(s0), .c_out(c0));
  two_bit_adder two_bit_adder_2 (.A(a1), .B(b1), .c_in(c0), .S(s1), .c_out(c1));
  two_bit_adder two_bit_adder_3 (.A(a2), .B(b2), .c_in(c1), .S(s2), .c_out(c2));
  two_bit_adder two_bit_adder_4 (.A(a3), .B(b3), .c_in(c2), .S(s3), .c_out(c3));
  two_bit_adder two_bit_adder_5 (.A(a4), .B(b4), .c_in(c3), .S(s4), .c_out(c4));
  two_bit_adder two_bit_adder_6 (.A(a5), .B(b5), .c_in(c4), .S(s5), .c_out(c5));
  two_bit_adder two_bit_adder_7 (.A(a6), .B(b6), .c_in(c5), .S(s6), .c_out(c6));
  two_bit_adder two_bit_adder_8 (.A(a7), .B(b7), .c_in(c6), .S(s7), .c_out(c_out));

  // Notes on the sheet:
  //   A - 8 bits
  //   B - 8 bits
endmodule
