// Logisim project conversor_bcd_sete.circ as structural Verilog: 2 circuits, main circuit main
module main (
  input  in_1,
  input  in_2,
  input  in_3,
  input  in_4
);

  wire l0, l1, l2, l3, l4, l5, l6, l7;

  conversor_bcd_sete_segimentos conversor_bcd_sete_segimentos_1 (
    .d0(in_1), .d1(in_2), .d2(in_3), .d3(in_4), .c(l2), .d(l1), .a(l6), .b(l7), .e(l0), .f(l5), .g(l4));
  _7_Segment_Display u_7_segment_display_1 (.g(l4), .f(l5), .a(l6), .b(l7), .e(l0), .d(l1), .c(l2), .dp(l3));
endmodule

module conversor_bcd_sete_segimentos (
  input  d0,
  input  d1,
  input  d2,
  input  d3,
  output c,
  output d,
  output a,
  output b,
  output e,
  output f,
  output g
);

  wire and_1_out, and_2_out, and_3_out, and_4_out, and_5_out, and_6_out, and_7_out, and_8_out, and_9_out,
       and_10_out, and_11_out, and_12_out, and_13_out, and_14_out, and_15_out, and_16_out, d0_b, d1_b, d2_b,
       d3_b;

  not not_1 (d0_b, d0);
  not not_2 (d1_b, d1);
  not not_3 (d2_b, d2);
  not not_4 (d3_b, d3);
  and and_1 (and_1_out, d0_b, d2_b);
  and and_2 (and_2_out, d0, d2);
  and and_3 (and_3_out, d0_b, d2_b);
  or or_1 (a, and_1_out, and_2_out, d3, d1);
  and and_4 (and_4_out, d1, d0_b);
  or or_2 (e, and_3_out, and_4_out);
  and and_5 (and_5_out, d2, d1_b);
  and and_6 (and_6_out, d1, d0);
  and and_7 (and_7_out, d2, d0_b);
  or or_3 (f, and_7_out, and_5_out, d3, and_9_out);
  and and_8 (and_8_out, d1_b, d0_b);
  and and_9 (and_9_out, d1_b, d0_b);
  or or_4 (b, and_6_out, and_8_out, d3, d2_b);
  and and_10 (and_10_out, d2, d1_b);
  or or_5 (g, and_10_out, d3, and_12_out, and_11_out);
  and and_11 (and_11_out, d2_b, d1);
  or or_6 (c, d3, d2, d1_b, d0);
  and and_12 (and_12_out, d1, d0_b);
  and and_13 (and_13_out, d1, d0_b);
  and and_14 (and_14_out, d2_b, d1, d0);
  or or_7 (d, and_13_out, and_14_out, and_15_out, and_16_out);
  and and_15 (and_15_out, d2, d1_b, d0);
  and and_16 (and_16_out, d2_b, d0_b);
endmodule
