// Logisim project decoder_2.circ as structural Verilog: 3 circuits, main circuit main
module main (
  input  in_1,
  input  in_2,
  input  in_3,
  input  in_4,
  output s0,
  output s1,
  output s2,
  output s3,
  output s4,
  output s5,
  output s6,
  output s7
);

  wire n03, n04, n10, n11, n13, n14, n15, n16, n22, n23, n25, n30, n31, n33, n36, n40, n41, n43, n46, n50,
       n53, n57, n63, n67, n70, n71, n73, n74, n75, n83, n90, n93;

  _7_Segment_Display u_7_segment_display_1 (.g(s4), .f(s5), .a(s6), .b(s7), .e(s0), .d(s1), .c(s2), .dp(s3));
  mux_big mux_big_1 (
    .b3(n90), .a3(1'b1), .b4(n70), .a4(1'b1), .b5(n50), .a5(n40), .b6(n30), .a6(1'b1), .b7(n10), .a7(1'b1),
    .s0(in_1), .s1(in_2), .s2(in_3), .s3(in_4), .s(s0));  // open: b0, a0, b1, a1, b2, a2
  mux_big mux_big_2 (
    .b3(1'b1), .a3(1'b1), .b4(n74), .a4(1'b1), .b5(1'b1), .a5(1'b1), .b6(1'b1), .a6(1'b1), .b7(n14),
    .a7(n04), .s0(in_1), .s1(in_2), .s2(in_3), .s3(in_4), .s(s4));  // open: b0, a0, b1, a1, b2, a2
  mux_big mux_big_3 (
    .b3(1'b1), .a3(1'b1), .b4(n71), .a4(1'b1), .b5(1'b1), .a5(n41), .b6(n31), .a6(1'b1), .b7(n11), .a7(1'b1),
    .s0(in_1), .s1(in_2), .s2(in_3), .s3(in_4), .s(s1));  // open: b0, a0, b1, a1, b2, a2
  mux_big mux_big_4 (
    .b3(1'b1), .a3(1'b1), .b4(n75), .a4(1'b1), .b5(1'b1), .a5(1'b1), .b6(1'b1), .a6(n25), .b7(n15),
    .a7(1'b1), .s0(in_1), .s1(in_2), .s2(in_3), .s3(in_4), .s(s5));  // open: b0, a0, b1, a1, b2, a2
  mux_big mux_big_5 (
    .b3(1'b1), .a3(1'b1), .b4(1'b1), .a4(1'b1), .b5(1'b1), .a5(1'b1), .b6(1'b1), .a6(n22), .b7(1'b1),
    .a7(1'b1), .s0(in_1), .s1(in_2), .s2(in_3), .s3(in_4), .s(s2));  // open: b0, a0, b1, a1, b2, a2
  mux_big mux_big_6 (
    .b3(1'b1), .a3(1'b1), .b4(1'b1), .a4(1'b1), .b5(1'b1), .a5(n46), .b6(n36), .a6(1'b1), .b7(n16),
    .a7(1'b1), .s0(in_1), .s1(in_2), .s2(in_3), .s3(in_4), .s(s6));  // open: b0, a0, b1, a1, b2, a2
  mux_big mux_big_7 (
    .b3(n93), .a3(n83), .b4(n73), .a4(n63), .b5(n53), .a5(n43), .b6(n33), .a6(n23), .b7(n13), .a7(n03),
    .s0(in_1), .s1(in_2), .s2(in_3), .s3(in_4), .s(s3));  // open: b0, a0, b1, a1, b2, a2
  mux_big mux_big_8 (
    .b3(1'b1), .a3(1'b1), .b4(1'b1), .a4(n67), .b5(n57), .a5(1'b1), .b6(1'b1), .a6(1'b1), .b7(1'b1),
    .a7(1'b1), .s0(in_1), .s1(in_2), .s2(in_3), .s3(in_4), .s(s7));  // open: b0, a0, b1, a1, b2, a2

  // Other names for the same wires on the sheet: l0 = s0; l1 = s1; l2 = s2; l3 = s3; l4 = s4; l5 = s5; l6 = s6;
  //   l7 = s7; s0_t = in_1; s1_t = in_2; s2_t = in_3; s3_t = in_4

  // Notes on the sheet:
  //   Numero 0
  //   Numero 1
  //   Numero 2
  //   Numero 3
  //   Numero 4
  //   Numero 5
  //   Numero 6
  //   Numero 7
  //   Numero 8
  //   Numero 9
endmodule

module mux_two_one (
  input  S,
  input  A,
  input  B,
  output X
);

  wire and_1_out, and_2_out, not_1_out;

  not not_1 (not_1_out, S);
  and and_1 (and_1_out, not_1_out, A);
  and and_2 (and_2_out, S, B);
  or or_1 (X, and_1_out, and_2_out);
endmodule

module mux_big (
  input  b0,
  input  a0,
  input  b1,
  input  a1,
  input  b2,
  input  a2,
  input  b3,
  input  a3,
  input  b4,
  input  a4,
  input  b5,
  input  a5,
  input  b6,
  input  a6,
  input  b7,
  input  a7,
  input  s0,
  input  s1,
  input  s2,
  input  s3,
  output s
);

  wire mux_two_one_1_x, mux_two_one_2_x, mux_two_one_3_x, mux_two_one_4_x, mux_two_one_5_x, mux_two_one_6_x,
       mux_two_one_7_x, mux_two_one_8_x, mux_two_one_10_x, mux_two_one_11_x, mux_two_one_12_x,
       mux_two_one_13_x, mux_two_one_14_x, mux_two_one_15_x;

  mux_two_one mux_two_one_1 (.S(s0), .A(a0), .B(b0), .X(mux_two_one_1_x));
  mux_two_one mux_two_one_2 (.S(s0), .A(a1), .B(b1), .X(mux_two_one_2_x));
  mux_two_one mux_two_one_3 (.S(s1), .A(mux_two_one_2_x), .B(mux_two_one_1_x), .X(mux_two_one_3_x));
  mux_two_one mux_two_one_4 (.S(s2), .A(mux_two_one_7_x), .B(mux_two_one_3_x), .X(mux_two_one_4_x));
  mux_two_one mux_two_one_5 (.S(s0), .A(a2), .B(b2), .X(mux_two_one_5_x));
  mux_two_one mux_two_one_6 (.S(s0), .A(a3), .B(b3), .X(mux_two_one_6_x));
  mux_two_one mux_two_one_7 (.S(s1), .A(mux_two_one_6_x), .B(mux_two_one_5_x), .X(mux_two_one_7_x));
  mux_two_one mux_two_one_8 (.S(s0), .A(a4), .B(b4), .X(mux_two_one_8_x));
  mux_two_one mux_two_one_9 (.S(s3), .A(mux_two_one_12_x), .B(mux_two_one_4_x), .X(s));
  mux_two_one mux_two_one_10 (.S(s0), .A(a5), .B(b5), .X(mux_two_one_10_x));
  mux_two_one mux_two_one_11 (.S(s1), .A(mux_two_one_10_x), .B(mux_two_one_8_x), .X(mux_two_one_11_x));
  mux_two_one mux_two_one_12 (.S(s2), .A(mux_two_one_15_x), .B(mux_two_one_11_x), .X(mux_two_one_12_x));
  mux_two_one mux_two_one_13 (.S(s0), .A(a6), .B(b6), .X(mux_two_one_13_x));
  mux_two_one mux_two_one_14 (.S(s0), .A(a7), .B(b7), .X(mux_two_one_14_x));
  mux_two_one mux_two_one_15 (.S(s1), .A(mux_two_one_14_x), .B(mux_two_one_13_x), .X(mux_two_one_15_x));

  // Notes on the sheet:
  //   A - 8 bits
  //   B - 8 bits
endmodule
