// Logisim project deslocador_esquerda_cir_8.circ as structural Verilog: 2 circuits, main circuit mux_two_one
module mux_two_one (
  input  S,
  input  A,
  input  B,
  output X
);

  wire and_1_out, and_2_out, not_1_out;

  not not_1 (not_1_out, S);
  and and_1 (and_1_out, not_1_out, A);
  and and_2 (and_2_out, S, B);
  or or_1 (X, and_1_out, and_2_out);
endmodule

module deslocador_esquerda (
  input  s0,
  input  s1,
  input  s2,
  input  s3,
  input  a0,
  input  a1,
  input  a2,
  input  a3,
  input  a4,
  input  a5,
  input  a6,
  input  a7,
  output out_13,
  output out_14,
  output out_15,
  output out_16,
  output out_17,
  output out_18,
  output out_19,
  output out_20
);

  wire mux_two_one_1_x, mux_two_one_2_x, mux_two_one_3_x, mux_two_one_4_x, mux_two_one_6_x, mux_two_one_7_x,
       mux_two_one_9_x, mux_two_one_10_x, mux_two_one_11_x, mux_two_one_12_x, mux_two_one_14_x,
       mux_two_one_15_x, mux_two_one_17_x, mux_two_one_18_x, mux_two_one_19_x, mux_two_one_21_x,
       mux_two_one_22_x, mux_two_one_23_x, mux_two_one_25_x, mux_two_one_26_x, mux_two_one_27_x,
       mux_two_one_29_x, mux_two_one_30_x, mux_two_one_31_x;

  mux_two_one mux_two_one_1 (.S(s3), .A(a7), .B(1'b0), .X(mux_two_one_1_x));
  mux_two_one mux_two_one_2 (.S(s2), .A(mux_two_one_1_x), .B(mux_two_one_17_x), .X(mux_two_one_2_x));
  mux_two_one mux_two_one_3 (.S(s3), .A(a6), .B(1'b0), .X(mux_two_one_3_x));
  mux_two_one mux_two_one_4 (.S(s1), .A(mux_two_one_2_x), .B(mux_two_one_10_x), .X(mux_two_one_4_x));
  mux_two_one mux_two_one_5 (.S(s0), .A(mux_two_one_4_x), .B(mux_two_one_7_x), .X(out_13));
  mux_two_one mux_two_one_6 (.S(s2), .A(mux_two_one_3_x), .B(mux_two_one_21_x), .X(mux_two_one_6_x));
  mux_two_one mux_two_one_7 (.S(s1), .A(mux_two_one_6_x), .B(mux_two_one_14_x), .X(mux_two_one_7_x));
  mux_two_one mux_two_one_8 (.S(s0), .A(mux_two_one_7_x), .B(mux_two_one_11_x), .X(out_14));
  mux_two_one mux_two_one_9 (.S(s3), .A(a5), .B(1'b0), .X(mux_two_one_9_x));
  mux_two_one mux_two_one_10 (.S(s2), .A(mux_two_one_9_x), .B(mux_two_one_25_x), .X(mux_two_one_10_x));
  mux_two_one mux_two_one_11 (.S(s1), .A(mux_two_one_10_x), .B(mux_two_one_18_x), .X(mux_two_one_11_x));
  mux_two_one mux_two_one_12 (.S(s3), .A(a4), .B(1'b0), .X(mux_two_one_12_x));
  mux_two_one mux_two_one_13 (.S(s0), .A(mux_two_one_11_x), .B(mux_two_one_15_x), .X(out_15));
  mux_two_one mux_two_one_14 (.S(s2), .A(mux_two_one_12_x), .B(mux_two_one_29_x), .X(mux_two_one_14_x));
  mux_two_one mux_two_one_15 (.S(s1), .A(mux_two_one_14_x), .B(mux_two_one_22_x), .X(mux_two_one_15_x));
  mux_two_one mux_two_one_16 (.S(s0), .A(mux_two_one_15_x), .B(mux_two_one_19_x), .X(out_16));
  mux_two_one mux_two_one_17 (.S(s3), .A(a3), .B(1'b0), .X(mux_two_one_17_x));
  mux_two_one mux_two_one_18 (.S(s2), .A(mux_two_one_17_x), .B(1'b0), .X(mux_two_one_18_x));
  mux_two_one mux_two_one_19 (.S(s1), .A(mux_two_one_18_x), .B(mux_two_one_26_x), .X(mux_two_one_19_x));
  mux_two_one mux_two_one_20 (.S(s0), .A(mux_two_one_19_x), .B(mux_two_one_23_x), .X(out_17));
  mux_two_one mux_two_one_21 (.S(s3), .A(a2), .B(1'b0), .X(mux_two_one_21_x));
  mux_two_one mux_two_one_22 (.S(s2), .A(mux_two_one_21_x), .B(1'b0), .X(mux_two_one_22_x));
  mux_two_one mux_two_one_23 (.S(s1), .A(mux_two_one_22_x), .B(mux_two_one_30_x), .X(mux_two_one_23_x));
  mux_two_one mux_two_one_24 (.S(s0), .A(mux_two_one_23_x), .B(mux_two_one_27_x), .X(out_18));
  mux_two_one mux_two_one_25 (.S(s3), .A(a1), .B(1'b0), .X(mux_two_one_25_x));
  mux_two_one mux_two_one_26 (.S(s1), .A(mux_two_one_25_x), .B(1'b0), .X(mux_two_one_26_x));
  mux_two_one mux_two_one_27 (.S(s1), .A(mux_two_one_26_x), .B(1'b0), .X(mux_two_one_27_x));
  mux_two_one mux_two_one_28 (.S(s0), .A(mux_two_one_27_x), .B(mux_two_one_31_x), .X(out_19));
  mux_two_one mux_two_one_29 (.S(s3), .A(a0), .B(1'b0), .X(mux_two_one_29_x));
  mux_two_one mux_two_one_30 (.S(s2), .A(mux_two_one_29_x), .B(1'b0), .X(mux_two_one_30_x));
  mux_two_one mux_two_one_31 (.S(s1), .A(mux_two_one_30_x), .B(1'b0), .X(mux_two_one_31_x));
  mux_two_one mux_two_one_32 (.S(s0), .A(mux_two_one_31_x), .B(1'b0), .X(out_20));
endmodule
