// Logisim project double_dabble.circ as structural Verilog: 8 circuits, main circuit main
module main (
  input  a0,
  input  a1,
  input  a2,
  input  a3,
  input  a4,
  input  a5,
  input  a6,
  input  a7,
  output s0,
  output s1,
  output s2,
  output s3,
  output s4,
  output s5,
  output s6,
  output s7,
  output s8,
  output s9,
  output s10,
  output s11
);

  wire four_or_three_1_s0, four_or_three_1_s1, four_or_three_1_s2, four_or_three_1_s3, four_or_three_2_s0,
       four_or_three_2_s1, four_or_three_2_s2, four_or_three_2_s3, four_or_three_3_s0, four_or_three_3_s1,
       four_or_three_3_s2, four_or_three_3_s3, four_or_three_4_s0, four_or_three_4_s1, four_or_three_4_s2,
       four_or_three_4_s3, four_or_three_5_s0, four_or_three_5_s1, four_or_three_5_s2, four_or_three_5_s3,
       four_or_three_6_s0, four_or_three_6_s1, four_or_three_6_s2, four_or_three_6_s3, four_or_three_7_s0,
       four_or_three_7_s1, four_or_three_7_s2, four_or_three_7_s3, four_or_three_8_s0, four_or_three_8_s1,
       four_or_three_8_s2, four_or_three_8_s3, four_or_three_9_s0, four_or_three_9_s1, four_or_three_9_s2,
       four_or_three_9_s3, undriven;

  four_or_three four_or_three_1 (
    .a0(a7), .s0(four_or_three_1_s0), .s1(four_or_three_1_s1), .s2(four_or_three_1_s2),
    .s3(four_or_three_1_s3));  // open: a1, a2, a3
  four_or_three four_or_three_2 (
    .a0(a6), .a1(four_or_three_1_s0), .a2(four_or_three_1_s1), .a3(four_or_three_1_s2),
    .s0(four_or_three_2_s0), .s1(four_or_three_2_s1), .s2(four_or_three_2_s2), .s3(four_or_three_2_s3));
  four_or_three four_or_three_3 (
    .a0(a5), .a1(four_or_three_2_s0), .a2(four_or_three_2_s1), .a3(four_or_three_2_s2),
    .s0(four_or_three_3_s0), .s1(four_or_three_3_s1), .s2(four_or_three_3_s2), .s3(four_or_three_3_s3));
  four_or_three four_or_three_4 (
    .a0(a4), .a1(four_or_three_3_s0), .a2(four_or_three_3_s1), .a3(four_or_three_3_s2),
    .s0(four_or_three_4_s0), .s1(four_or_three_4_s1), .s2(four_or_three_4_s2), .s3(four_or_three_4_s3));
  four_or_three four_or_three_5 (
    .a0(four_or_three_3_s3), .a1(four_or_three_2_s3), .a2(four_or_three_1_s3), .s0(four_or_three_5_s0),
    .s1(four_or_three_5_s1), .s2(four_or_three_5_s2), .s3(four_or_three_5_s3));  // open: a3
  four_or_three four_or_three_6 (
    .a0(a3), .a1(four_or_three_4_s0), .a2(four_or_three_4_s1), .a3(four_or_three_4_s2),
    .s0(four_or_three_6_s0), .s1(four_or_three_6_s1), .s2(four_or_three_6_s2), .s3(four_or_three_6_s3));
  four_or_three four_or_three_7 (
    .a0(four_or_three_4_s3), .a1(four_or_three_5_s0), .a2(four_or_three_5_s1), .a3(four_or_three_5_s2),
    .s0(four_or_three_7_s0), .s1(four_or_three_7_s1), .s2(four_or_three_7_s2), .s3(four_or_three_7_s3));
  four_or_three four_or_three_8 (
    .a0(a2), .a1(four_or_three_6_s0), .a2(four_or_three_6_s1), .a3(four_or_three_6_s2),
    .s0(four_or_three_8_s0), .s1(four_or_three_8_s1), .s2(four_or_three_8_s2), .s3(four_or_three_8_s3));
  four_or_three four_or_three_9 (
    .a0(four_or_three_6_s3), .a1(four_or_three_7_s0), .a2(four_or_three_7_s1), .a3(four_or_three_7_s2),
    .s0(four_or_three_9_s0), .s1(four_or_three_9_s1), .s2(four_or_three_9_s2), .s3(four_or_three_9_s3));
  four_or_three four_or_three_10 (
    .a0(a1), .a1(four_or_three_8_s0), .a2(four_or_three_8_s1), .a3(four_or_three_8_s2), .s0(s1), .s1(s2),
    .s2(s3), .s3(s4));
  four_or_three four_or_three_11 (
    .a0(four_or_three_8_s3), .a1(four_or_three_9_s0), .a2(four_or_three_9_s1), .a3(four_or_three_9_s2),
    .s0(s5), .s1(s6), .s2(s7), .s3(s8));
  four_or_three four_or_three_12 (
    .a0(four_or_three_9_s3), .a1(four_or_three_7_s3), .a2(four_or_three_5_s3), .a3(undriven), .s0(s9),
    .s1(s10), .s2(s11));  // open: s3

  assign s0 = a0;

  // Notes on the sheet:
  //   A - 8 bits
endmodule

module two_bit_adder (
  input  A,
  input  B,
  input  c_in,
  output S,
  output c_out
);

  wire and_1_out, and_2_out, xor_1_out;

  xor xor_1 (xor_1_out, A, B);
  and and_1 (and_1_out, A, B);
  xor xor_2 (S, xor_1_out, c_in);
  and and_2 (and_2_out, c_in, xor_1_out);
  or or_1 (c_out, and_2_out, and_1_out);
endmodule

module for_bit_adder (
  input  a0,
  input  a1,
  input  a2,
  input  a3,
  input  c_in,
  input  b0,
  input  b1,
  input  b2,
  input  b3,
  output s0,
  output s1,
  output s2,
  output c_out,
  output s3
);

  wire c0, c1, c2;

  two_bit_adder two_bit_adder_1 (.A(a0), .B(b0), .c_in(c_in), .S(s0), .c_out(c0));
  two_bit_adder two_bit_adder_2 (.A(a1), .B(b1), .c_in(c0), .S(s1), .c_out(c1));
  two_bit_adder two_bit_adder_3 (.A(a2), .B(b2), .c_in(c1), .S(s2), .c_out(c2));
  two_bit_adder two_bit_adder_4 (.A(a3), .B(b3), .c_in(c2), .S(s3), .c_out(c_out));

  // Notes on the sheet:
  //   A - 8 bits
  //   B - 8 bits
endmodule

module compadador (
  input  in_a_b,
  input  a_in,
  input  b_in,
  input  in_b0,
  input  in_a0,
  output a_b,
  output a0,
  output b0
);

  wire and_1_out, and_2_out, and_3_out, and_4_out, not_1_out, not_2_out, xnor_1_out;

  not not_1 (not_1_out, b_in);
  not not_2 (not_2_out, a_in);
  xnor xnor_1 (xnor_1_out, a_in, b_in);
  and and_1 (and_1_out, not_1_out, a_in);
  and and_2 (and_2_out, b_in, not_2_out);
  and and_3 (and_3_out, in_a_b, and_1_out);
  and and_4 (and_4_out, in_a_b, and_2_out);
  and and_5 (a_b, in_a_b, xnor_1_out);
  or or_1 (a0, and_3_out, in_a0);
  or or_2 (b0, and_4_out, in_b0);
endmodule

module four_bit_comparator (
  input  b0,
  input  a0,
  input  b1,
  input  a1,
  input  b2,
  input  a2,
  input  b3,
  input  a3,
  output a_b,
  output b_out,
  output a_out
);

  wire compadador_1_a0, compadador_1_a_b, compadador_1_b0, compadador_2_a0, compadador_2_a_b,
       compadador_2_b0, compadador_3_a0, compadador_3_a_b, compadador_3_b0;

  compadador compadador_1 (
    .in_a_b(1'b1), .a_in(b0), .b_in(a0), .a_b(compadador_1_a_b), .a0(compadador_1_a0), .b0(compadador_1_b0));  // open: in_b0, in_a0
  compadador compadador_2 (
    .in_a_b(compadador_1_a_b), .a_in(b1), .b_in(a1), .in_b0(compadador_1_b0), .in_a0(compadador_1_a0),
    .a_b(compadador_2_a_b), .a0(compadador_2_a0), .b0(compadador_2_b0));
  compadador compadador_3 (
    .in_a_b(compadador_2_a_b), .a_in(b2), .b_in(a2), .in_b0(compadador_2_b0), .in_a0(compadador_2_a0),
    .a_b(compadador_3_a_b), .a0(compadador_3_a0), .b0(compadador_3_b0));
  compadador compadador_4 (
    .in_a_b(compadador_3_a_b), .a_in(b3), .b_in(a3), .in_b0(compadador_3_b0), .in_a0(compadador_3_a0),
    .a_b(a_b), .a0(b_out), .b0(a_out));
endmodule

module four_or_three (
  input  a0,
  input  a1,
  input  a2,
  input  a3,
  output s0,
  output s1,
  output s2,
  output s3
);

  wire b0, b1, b3, b32, b33, four_bit_comparator_1_a_out, s0_t, s1_t, s2_t, s3_t;

  four_bit_comparator four_bit_comparator_1 (
    .b0(b3), .a0(a3), .b1(1'b1), .a1(a2), .b2(b1), .a2(a1), .b3(b0), .a3(a0),
    .a_out(four_bit_comparator_1_a_out));  // open: a_b, b_out
  for_bit_adder for_bit_adder_1 (
    .a0(a0), .a1(a1), .a2(a2), .a3(a3), .b0(1'b1), .b1(1'b1), .b2(b32), .b3(b33), .s0(s0_t), .s1(s1_t),
    .s2(s2_t), .s3(s3_t));  // open: c_in, c_out
  two_four_mux two_four_mux_1 (
    .s(four_bit_comparator_1_a_out), .a0(a0), .a1(a1), .a2(a2), .a3(a3), .b1(s0_t), .b2(s1_t), .b3(s2_t),
    .b4(s3_t), .s0(s0), .s1(s1), .s2(s2), .s3(s3));

  // Notes on the sheet:
  //   A - 4 bits
  //   4 - 4 bits
  //   3 - 4 bits
endmodule

module two_mux (
  input  S,
  input  A,
  input  B,
  output X
);

  wire and_1_out, and_2_out, not_1_out;

  not not_1 (not_1_out, S);
  and and_1 (and_1_out, not_1_out, A);
  and and_2 (and_2_out, S, B);
  or or_1 (X, and_1_out, and_2_out);
endmodule

module two_four_mux (
  input  s,
  input  a0,
  input  a1,
  input  a2,
  input  a3,
  input  b1,
  input  b2,
  input  b3,
  input  b4,
  output s0,
  output s1,
  output s2,
  output s3
);

  two_mux two_mux_1 (.S(s), .A(a0), .B(b1), .X(s0));
  two_mux two_mux_2 (.S(s), .A(a1), .B(b2), .X(s1));
  two_mux two_mux_3 (.S(s), .A(a2), .B(b3), .X(s2));
  two_mux two_mux_4 (.S(s), .A(a3), .B(b4), .X(s3));

  // Other names for the same wires on the sheet: b0 = b1; b1_t = b2; b2_t = b3; b3_t = b4
endmodule
