// Logisim project mutiplicador.circ as structural Verilog
module multiplicador (
  input  b0,
  input  b1,
  input  b2,
  input  b3,
  input  b4,
  input  b5,
  input  b6,
  input  b7,
  input  a0,
  input  a1,
  input  a2,
  input  a3,
  input  a4,
  input  a5,
  input  a6,
  input  a7,
  output r15,
  output r14,
  output r13,
  output r12,
  output r11,
  output r10,
  output r9,
  output r8,
  output r7,
  output r6,
  output r5,
  output r4,
  output r3,
  output r2,
  output r1,
  output r0
);

  wire m00, m01, m02, m03, m04, m05, m06, m07, m10, m11, m12, m13, m14, m15, m16, m17, m20, m21, m22, m23,
       m24, m25, m26, m27, m30, m31, m32, m33, m34, m35, m36, m37, m40, m41, m42, m43, m44, m45, m46, m47,
       m50, m51, m52, m53, m54, m55, m56, m57, m60, m61, m62, m63, m64, m65, m66, m67, m70, m71, m72, m73,
       m74, m75, m76, m77, sixteen_adder_1_s0, sixteen_adder_1_s1, sixteen_adder_1_s2, sixteen_adder_1_s3,
       sixteen_adder_1_s4, sixteen_adder_1_s5, sixteen_adder_1_s6, sixteen_adder_1_s7, sixteen_adder_1_s8,
       sixteen_adder_1_s9, sixteen_adder_1_s10, sixteen_adder_1_s11, sixteen_adder_1_s12,
       sixteen_adder_1_s13, sixteen_adder_1_s14, sixteen_adder_1_s15, sixteen_adder_2_s0, sixteen_adder_2_s1,
       sixteen_adder_2_s2, sixteen_adder_2_s3, sixteen_adder_2_s4, sixteen_adder_2_s5, sixteen_adder_2_s6,
       sixteen_adder_2_s7, sixteen_adder_2_s8, sixteen_adder_2_s9, sixteen_adder_2_s10, sixteen_adder_2_s11,
       sixteen_adder_2_s12, sixteen_adder_2_s13, sixteen_adder_2_s14, sixteen_adder_2_s15,
       sixteen_adder_3_s0, sixteen_adder_3_s1, sixteen_adder_3_s2, sixteen_adder_3_s3, sixteen_adder_3_s4,
       sixteen_adder_3_s5, sixteen_adder_3_s6, sixteen_adder_3_s7, sixteen_adder_3_s8, sixteen_adder_3_s9,
       sixteen_adder_3_s10, sixteen_adder_3_s11, sixteen_adder_3_s12, sixteen_adder_3_s13,
       sixteen_adder_3_s14, sixteen_adder_3_s15, sixteen_adder_4_s0, sixteen_adder_4_s1, sixteen_adder_4_s2,
       sixteen_adder_4_s3, sixteen_adder_4_s4, sixteen_adder_4_s5, sixteen_adder_4_s6, sixteen_adder_4_s7,
       sixteen_adder_4_s8, sixteen_adder_4_s9, sixteen_adder_4_s10, sixteen_adder_4_s11, sixteen_adder_4_s12,
       sixteen_adder_4_s13, sixteen_adder_4_s14, sixteen_adder_4_s15, sixteen_adder_5_s0, sixteen_adder_5_s1,
       sixteen_adder_5_s2, sixteen_adder_5_s3, sixteen_adder_5_s4, sixteen_adder_5_s5, sixteen_adder_5_s6,
       sixteen_adder_5_s7, sixteen_adder_5_s8, sixteen_adder_5_s9, sixteen_adder_5_s10, sixteen_adder_5_s11,
       sixteen_adder_5_s12, sixteen_adder_5_s13, sixteen_adder_5_s14, sixteen_adder_5_s15,
       sixteen_adder_6_s0, sixteen_adder_6_s1, sixteen_adder_6_s2, sixteen_adder_6_s3, sixteen_adder_6_s4,
       sixteen_adder_6_s5, sixteen_adder_6_s6, sixteen_adder_6_s7, sixteen_adder_6_s8, sixteen_adder_6_s9,
       sixteen_adder_6_s10, sixteen_adder_6_s11, sixteen_adder_6_s12, sixteen_adder_6_s13,
       sixteen_adder_6_s14, sixteen_adder_6_s15, sixteen_adder_7_s0, sixteen_adder_7_s1, sixteen_adder_7_s2,
       sixteen_adder_7_s3, sixteen_adder_7_s4, sixteen_adder_7_s5, sixteen_adder_7_s6, sixteen_adder_7_s7,
       sixteen_adder_7_s8, sixteen_adder_7_s9, sixteen_adder_7_s10, sixteen_adder_7_s11, sixteen_adder_7_s12,
       sixteen_adder_7_s13, sixteen_adder_7_s14, sixteen_adder_7_s15;

  and and_1 (m00, a0, b0);
  and and_2 (m10, a1, b0);
  and and_3 (m20, a2, b0);
  and and_4 (m30, a3, b0);
  and and_5 (m40, a4, b0);
  and and_6 (m50, a5, b0);
  and and_7 (m60, a6, b0);
  and and_8 (m70, a7, b0);
  and and_9 (m01, a0, b1);
  and and_10 (m11, a1, b1);
  and and_11 (m21, a2, b1);
  and and_12 (m31, a3, b1);
  and and_13 (m41, a4, b1);
  and and_14 (m51, a5, b1);
  and and_15 (m61, a6, b1);
  and and_16 (m71, a7, b1);
  and and_17 (m02, a0, b2);
  and and_18 (m12, a1, b2);
  and and_19 (m22, a2, b2);
  and and_20 (m32, a3, b2);
  and and_21 (m42, a4, b2);
  and and_22 (m52, a5, b2);
  and and_23 (m62, a6, b2);
  and and_24 (m72, a7, b2);
  and and_25 (m03, a0, b3);
  and and_26 (m13, a1, b3);
  and and_27 (m23, a2, b3);
  and and_28 (m33, a3, b3);
  and and_29 (m43, a4, b3);
  and and_30 (m53, a5, b3);
  and and_31 (m63, a6, b3);
  and and_32 (m73, a7, b3);
  and and_33 (m04, a0, b4);
  and and_34 (m14, a1, b4);
  and and_35 (m24, a2, b4);
  and and_36 (m34, a3, b4);
  and and_37 (m44, a4, b4);
  and and_38 (m54, a5, b4);
  and and_39 (m64, a6, b4);
  and and_40 (m74, a7, b4);
  and and_41 (m05, a0, b5);
  and and_42 (m15, a1, b5);
  and and_43 (m25, a2, b5);
  and and_44 (m35, a3, b5);
  and and_45 (m45, a4, b5);
  and and_46 (m55, a5, b5);
  and and_47 (m65, a6, b5);
  and and_48 (m75, a7, b5);
  and and_49 (m06, a0, b6);
  and and_50 (m16, a1, b6);
  and and_51 (m26, a2, b6);
  and and_52 (m36, a3, b6);
  and and_53 (m46, a4, b6);
  and and_54 (m56, a5, b6);
  and and_55 (m66, a6, b6);
  and and_56 (m76, a7, b6);
  and and_57 (m07, a0, b7);
  and and_58 (m17, a1, b7);
  and and_59 (m27, a2, b7);
  and and_60 (m37, a3, b7);
  and and_61 (m47, a4, b7);
  and and_62 (m57, a5, b7);
  and and_63 (m67, a6, b7);
  and and_64 (m77, a7, b7);
  sixteen_adder sixteen_adder_1 (
    .a0(m00), .a1(m01), .a2(m02), .a3(m03), .a4(m04), .a5(m05), .a6(m06), .a7(m07), .b1(m10), .b2(m11),
    .b3(m12), .b4(m13), .b5(m14), .b6(m15), .b7(m16), .b8(m17), .s0(sixteen_adder_1_s0),
    .s1(sixteen_adder_1_s1), .s2(sixteen_adder_1_s2), .s3(sixteen_adder_1_s3), .s4(sixteen_adder_1_s4),
    .s5(sixteen_adder_1_s5), .s6(sixteen_adder_1_s6), .s7(sixteen_adder_1_s7), .s8(sixteen_adder_1_s8),
    .s9(sixteen_adder_1_s9), .s10(sixteen_adder_1_s10), .s11(sixteen_adder_1_s11), .s12(sixteen_adder_1_s12),
    .s13(sixteen_adder_1_s13), .s14(sixteen_adder_1_s14), .s15(sixteen_adder_1_s15));  // open: c_in, a8, a9, a10, a11, a12, a13, a14, a15, b0, b9, b10, b11, b12, b13, b14, b16, c_out
  sixteen_adder sixteen_adder_2 (
    .a2(m20), .a3(m21), .a4(m22), .a5(m23), .a6(m24), .a7(m25), .a8(m26), .a9(m27), .b0(sixteen_adder_1_s0),
    .b1(sixteen_adder_1_s1), .b2(sixteen_adder_1_s2), .b3(sixteen_adder_1_s3), .b4(sixteen_adder_1_s4),
    .b5(sixteen_adder_1_s5), .b6(sixteen_adder_1_s6), .b7(sixteen_adder_1_s7), .b8(sixteen_adder_1_s8),
    .b9(sixteen_adder_1_s9), .b10(sixteen_adder_1_s10), .b11(sixteen_adder_1_s11), .b12(sixteen_adder_1_s12),
    .b13(sixteen_adder_1_s13), .b14(sixteen_adder_1_s14), .b16(sixteen_adder_1_s15), .s0(sixteen_adder_2_s0),
    .s1(sixteen_adder_2_s1), .s2(sixteen_adder_2_s2), .s3(sixteen_adder_2_s3), .s4(sixteen_adder_2_s4),
    .s5(sixteen_adder_2_s5), .s6(sixteen_adder_2_s6), .s7(sixteen_adder_2_s7), .s8(sixteen_adder_2_s8),
    .s9(sixteen_adder_2_s9), .s10(sixteen_adder_2_s10), .s11(sixteen_adder_2_s11), .s12(sixteen_adder_2_s12),
    .s13(sixteen_adder_2_s13), .s14(sixteen_adder_2_s14), .s15(sixteen_adder_2_s15));  // open: a0, a1, c_in, a10, a11, a12, a13, a14, a15, c_out
  sixteen_adder sixteen_adder_3 (
    .a3(m30), .a4(m31), .a5(m32), .a6(m33), .a7(m34), .a8(m35), .a9(m36), .a10(m37), .b0(sixteen_adder_2_s0),
    .b1(sixteen_adder_2_s1), .b2(sixteen_adder_2_s2), .b3(sixteen_adder_2_s3), .b4(sixteen_adder_2_s4),
    .b5(sixteen_adder_2_s5), .b6(sixteen_adder_2_s6), .b7(sixteen_adder_2_s7), .b8(sixteen_adder_2_s8),
    .b9(sixteen_adder_2_s9), .b10(sixteen_adder_2_s10), .b11(sixteen_adder_2_s11), .b12(sixteen_adder_2_s12),
    .b13(sixteen_adder_2_s13), .b14(sixteen_adder_2_s14), .b16(sixteen_adder_2_s15), .s0(sixteen_adder_3_s0),
    .s1(sixteen_adder_3_s1), .s2(sixteen_adder_3_s2), .s3(sixteen_adder_3_s3), .s4(sixteen_adder_3_s4),
    .s5(sixteen_adder_3_s5), .s6(sixteen_adder_3_s6), .s7(sixteen_adder_3_s7), .s8(sixteen_adder_3_s8),
    .s9(sixteen_adder_3_s9), .s10(sixteen_adder_3_s10), .s11(sixteen_adder_3_s11), .s12(sixteen_adder_3_s12),
    .s13(sixteen_adder_3_s13), .s14(sixteen_adder_3_s14), .s15(sixteen_adder_3_s15));  // open: a0, a1, a2, c_in, a11, a12, a13, a14, a15, c_out
  sixteen_adder sixteen_adder_4 (
    .a4(m40), .a5(m41), .a6(m42), .a7(m43), .a8(m44), .a9(m45), .a10(m46), .a11(m47),
    .b0(sixteen_adder_3_s0), .b1(sixteen_adder_3_s1), .b2(sixteen_adder_3_s2), .b3(sixteen_adder_3_s3),
    .b4(sixteen_adder_3_s4), .b5(sixteen_adder_3_s5), .b6(sixteen_adder_3_s6), .b7(sixteen_adder_3_s7),
    .b8(sixteen_adder_3_s8), .b9(sixteen_adder_3_s9), .b10(sixteen_adder_3_s10), .b11(sixteen_adder_3_s11),
    .b12(sixteen_adder_3_s12), .b13(sixteen_adder_3_s13), .b14(sixteen_adder_3_s14),
    .b16(sixteen_adder_3_s15), .s0(sixteen_adder_4_s0), .s1(sixteen_adder_4_s1), .s2(sixteen_adder_4_s2),
    .s3(sixteen_adder_4_s3), .s4(sixteen_adder_4_s4), .s5(sixteen_adder_4_s5), .s6(sixteen_adder_4_s6),
    .s7(sixteen_adder_4_s7), .s8(sixteen_adder_4_s8), .s9(sixteen_adder_4_s9), .s10(sixteen_adder_4_s10),
    .s11(sixteen_adder_4_s11), .s12(sixteen_adder_4_s12), .s13(sixteen_adder_4_s13),
    .s14(sixteen_adder_4_s14), .s15(sixteen_adder_4_s15));  // open: a0, a1, a2, a3, c_in, a12, a13, a14, a15, c_out
  sixteen_adder sixteen_adder_5 (
    .a5(m50), .a6(m51), .a7(m52), .a8(m53), .a9(m54), .a10(m55), .a11(m56), .a12(m57),
    .b0(sixteen_adder_4_s0), .b1(sixteen_adder_4_s1), .b2(sixteen_adder_4_s2), .b3(sixteen_adder_4_s3),
    .b4(sixteen_adder_4_s4), .b5(sixteen_adder_4_s5), .b6(sixteen_adder_4_s6), .b7(sixteen_adder_4_s7),
    .b8(sixteen_adder_4_s8), .b9(sixteen_adder_4_s9), .b10(sixteen_adder_4_s10), .b11(sixteen_adder_4_s11),
    .b12(sixteen_adder_4_s12), .b13(sixteen_adder_4_s13), .b14(sixteen_adder_4_s14),
    .b16(sixteen_adder_4_s15), .s0(sixteen_adder_5_s0), .s1(sixteen_adder_5_s1), .s2(sixteen_adder_5_s2),
    .s3(sixteen_adder_5_s3), .s4(sixteen_adder_5_s4), .s5(sixteen_adder_5_s5), .s6(sixteen_adder_5_s6),
    .s7(sixteen_adder_5_s7), .s8(sixteen_adder_5_s8), .s9(sixteen_adder_5_s9), .s10(sixteen_adder_5_s10),
    .s11(sixteen_adder_5_s11), .s12(sixteen_adder_5_s12), .s13(sixteen_adder_5_s13),
    .s14(sixteen_adder_5_s14), .s15(sixteen_adder_5_s15));  // open: a0, a1, a2, a3, c_in, a4, a13, a14, a15, c_out
  sixteen_adder sixteen_adder_6 (
    .a6(m60), .a7(m61), .a8(m62), .a9(m63), .a10(m64), .a11(m65), .a12(m66), .a13(m67),
    .b0(sixteen_adder_5_s0), .b1(sixteen_adder_5_s1), .b2(sixteen_adder_5_s2), .b3(sixteen_adder_5_s3),
    .b4(sixteen_adder_5_s4), .b5(sixteen_adder_5_s5), .b6(sixteen_adder_5_s6), .b7(sixteen_adder_5_s7),
    .b8(sixteen_adder_5_s8), .b9(sixteen_adder_5_s9), .b10(sixteen_adder_5_s10), .b11(sixteen_adder_5_s11),
    .b12(sixteen_adder_5_s12), .b13(sixteen_adder_5_s13), .b14(sixteen_adder_5_s14),
    .b16(sixteen_adder_5_s15), .s0(sixteen_adder_6_s0), .s1(sixteen_adder_6_s1), .s2(sixteen_adder_6_s2),
    .s3(sixteen_adder_6_s3), .s4(sixteen_adder_6_s4), .s5(sixteen_adder_6_s5), .s6(sixteen_adder_6_s6),
    .s7(sixteen_adder_6_s7), .s8(sixteen_adder_6_s8), .s9(sixteen_adder_6_s9), .s10(sixteen_adder_6_s10),
    .s11(sixteen_adder_6_s11), .s12(sixteen_adder_6_s12), .s13(sixteen_adder_6_s13),
    .s14(sixteen_adder_6_s14), .s15(sixteen_adder_6_s15));  // open: a0, a1, a2, a3, c_in, a4, a5, a14, a15, c_out
  sixteen_adder sixteen_adder_7 (
    .a7(m60), .a8(m61), .a9(m62), .a10(m63), .a11(m64), .a12(m65), .a13(m66), .a14(m67),
    .b0(sixteen_adder_6_s0), .b1(sixteen_adder_6_s1), .b2(sixteen_adder_6_s2), .b3(sixteen_adder_6_s3),
    .b4(sixteen_adder_6_s4), .b5(sixteen_adder_6_s5), .b6(sixteen_adder_6_s6), .b7(sixteen_adder_6_s7),
    .b8(sixteen_adder_6_s8), .b9(sixteen_adder_6_s9), .b10(sixteen_adder_6_s10), .b11(sixteen_adder_6_s11),
    .b12(sixteen_adder_6_s12), .b13(sixteen_adder_6_s13), .b14(sixteen_adder_6_s14),
    .b16(sixteen_adder_6_s15), .s0(sixteen_adder_7_s0), .s1(sixteen_adder_7_s1), .s2(sixteen_adder_7_s2),
    .s3(sixteen_adder_7_s3), .s4(sixteen_adder_7_s4), .s5(sixteen_adder_7_s5), .s6(sixteen_adder_7_s6),
    .s7(sixteen_adder_7_s7), .s8(sixteen_adder_7_s8), .s9(sixteen_adder_7_s9), .s10(sixteen_adder_7_s10),
    .s11(sixteen_adder_7_s11), .s12(sixteen_adder_7_s12), .s13(sixteen_adder_7_s13),
    .s14(sixteen_adder_7_s14), .s15(sixteen_adder_7_s15));  // open: a0, a1, a2, a3, c_in, a4, a5, a6, a15, c_out
  sixteen_adder sixteen_adder_8 (
    .a8(m70), .a9(m71), .a10(m72), .a11(m73), .a12(m74), .a13(m75), .a14(m76), .a15(m77),
    .b0(sixteen_adder_7_s0), .b1(sixteen_adder_7_s1), .b2(sixteen_adder_7_s2), .b3(sixteen_adder_7_s3),
    .b4(sixteen_adder_7_s4), .b5(sixteen_adder_7_s5), .b6(sixteen_adder_7_s6), .b7(sixteen_adder_7_s7),
    .b8(sixteen_adder_7_s8), .b9(sixteen_adder_7_s9), .b10(sixteen_adder_7_s10), .b11(sixteen_adder_7_s11),
    .b12(sixteen_adder_7_s12), .b13(sixteen_adder_7_s13), .b14(sixteen_adder_7_s14),
    .b16(sixteen_adder_7_s15), .s0(r0), .s1(r1), .s2(r2), .s3(r3), .s4(r4), .s5(r5), .s6(r6), .s7(r7),
    .s8(r8), .s9(r9), .s10(r10), .s11(r11), .s12(r12), .s13(r13), .s14(r14), .s15(r15));  // open: a0, a1, a2, a3, c_in, a4, a5, a6, a7, c_out
endmodule

module two_bit_adder (
  input  A,
  input  B,
  input  c_in,
  output S,
  output c_out
);

  wire and_1_out, and_2_out, xor_1_out;

  xor xor_1 (xor_1_out, A, B);
  and and_1 (and_1_out, A, B);
  xor xor_2 (S, xor_1_out, c_in);
  and and_2 (and_2_out, c_in, xor_1_out);
  or or_1 (c_out, and_2_out, and_1_out);
endmodule

module sixteen_adder (
  input  a0,
  input  a1,
  input  a2,
  input  a3,
  input  c_in,
  input  a4,
  input  a5,
  input  a6,
  input  a7,
  input  a8,
  input  a9,
  input  a10,
  input  a11,
  input  a12,
  input  a13,
  input  a14,
  input  a15,
  input  b0,
  input  b1,
  input  b2,
  input  b3,
  input  b4,
  input  b5,
  input  b6,
  input  b7,
  input  b8,
  input  b9,
  input  b10,
  input  b11,
  input  b12,
  input  b13,
  input  b14,
  input  b16,
  output s0,
  output s1,
  output s2,
  output s3,
  output s4,
  output s5,
  output s6,
  output s7,
  output s8,
  output s9,
  output s10,
  output s11,
  output s12,
  output s13,
  output s14,
  output s15,
  output c_out
);

  wire c0, c1, c2, c3, c4, c5, c6, c7, c8, c9, c10, c11, c12, c13, c14;

  two_bit_adder two_bit_adder_1 (.A(a0), .B(b0), .c_in(c_in), .S(s0), .c_out(c0));
  two_bit_adder two_bit_adder_2 (.A(a1), .B(b1), .c_in(c0), .S(s1), .c_out(c1));
  two_bit_adder two_bit_adder_3 (.A(a2), .B(b2), .c_in(c1), .S(s2), .c_out(c2));
  two_bit_adder two_bit_adder_4 (.A(a3), .B(b3), .c_in(c2), .S(s3), .c_out(c3));
  two_bit_adder two_bit_adder_5 (.A(a4), .B(b4), .c_in(c3), .S(s4), .c_out(c4));
  two_bit_adder two_bit_adder_6 (.A(a5), .B(b5), .c_in(c4), .S(s5), .c_out(c5));
  two_bit_adder two_bit_adder_7 (.A(a6), .B(b6), .c_in(c5), .S(s6), .c_out(c6));
  two_bit_adder two_bit_adder_8 (.A(a7), .B(b7), .c_in(c6), .S(s7), .c_out(c7));
  two_bit_adder two_bit_adder_9 (.A(a8), .B(b8), .c_in(c7), .S(s8), .c_out(c8));
  two_bit_adder two_bit_adder_10 (.A(a9), .B(b9), .c_in(c8), .S(s9), .c_out(c9));
  two_bit_adder two_bit_adder_11 (.A(a10), .B(b10), .c_in(c9), .S(s10), .c_out(c10));
  two_bit_adder two_bit_adder_12 (.A(a11), .B(b11), .c_in(c10), .S(s11), .c_out(c11));
  two_bit_adder two_bit_adder_13 (.A(a12), .B(b12), .c_in(c11), .S(s12), .c_out(c12));
  two_bit_adder two_bit_adder_14 (.A(a13), .B(b13), .c_in(c12), .S(s13), .c_out(c13));
  two_bit_adder two_bit_adder_15 (.A(a14), .B(b14), .c_in(c13), .S(s14), .c_out(c14));
  two_bit_adder two_bit_adder_16 (.A(a15), .B(b16), .c_in(c14), .S(s15), .c_out(c_out));

  // Other names for the same wires on the sheet: b15 = b16

  // Notes on the sheet:
  //   A - 16 bits
  //   B - 16 bits
endmodule
