// Logisim project mux.circ as structural Verilog: 2 circuits, main circuit main
module main (
  input  in_1,
  input  in_2,
  input  in_3,
  input  in_4
);
endmodule

module mux_two (
  input  S,
  input  A,
  input  B,
  output X
);

  wire and_1_out, and_2_out, not_1_out;

  _7_Segment_Display u_7_segment_display_1 (.g(1'b1), .f(1'b1), .a(1'b1));  // open: b, e, d, c, dp
  not not_1 (not_1_out, S);
  and and_1 (and_1_out, not_1_out, A);
  and and_2 (and_2_out, S, B);
  or or_1 (X, and_1_out, and_2_out);
endmodule
