// Logisim project mux_16_8.circ as structural Verilog
module mux_two_one (
  input  S,
  input  A,
  input  B,
  output X
);

  wire and_1_out, and_2_out, not_1_out;

  not not_1 (not_1_out, S);
  and and_1 (and_1_out, not_1_out, A);
  and and_2 (and_2_out, S, B);
  or or_1 (X, and_1_out, and_2_out);
endmodule

module deslocador_8bits (
);

  mux_two_one mux_two_one_1 ();  // open: S, A, B, X
  mux_two_one mux_two_one_2 ();  // open: S, A, B, X
endmodule
