// Logisim project contador.circ as structural Verilog
module registrador (
  input  a0,
  input  s0,
  input  a1,
  input  s1,
  input  a2,
  input  s2,
  input  a3,
  input  s3,
  input  s,
  input  clock,
  input  r,
  output q0,
  output q1,
  output q2,
  output q3
);

  wire multiplexer_1_out, multiplexer_2_out, multiplexer_3_out, multiplexer_4_out;

  D_Flip_Flop d_ff_1 (.D(multiplexer_1_out), .clk(clock), .Q(q0), .preset(s0), .reset(r));  // open: Qn
  Multiplexer multiplexer_1 (.in0(a0), .in1(q0), .out(multiplexer_1_out), .sel(s));
  Multiplexer multiplexer_2 (.in0(a1), .in1(q1), .out(multiplexer_2_out), .sel(s));
  D_Flip_Flop d_ff_2 (.D(multiplexer_2_out), .clk(clock), .Q(q1), .preset(s1), .reset(r));  // open: Qn
  Multiplexer multiplexer_3 (.in0(a2), .in1(q2), .out(multiplexer_3_out), .sel(s));
  D_Flip_Flop d_ff_3 (.D(multiplexer_3_out), .clk(clock), .Q(q2), .preset(s2), .reset(r));  // open: Qn
  Multiplexer multiplexer_4 (.in0(a3), .in1(q3), .out(multiplexer_4_out), .sel(s));
  D_Flip_Flop d_ff_4 (.D(multiplexer_4_out), .clk(clock), .Q(q3), .preset(s3), .reset(r));  // open: Qn
endmodule

module somador_bcd (
  input  a0,
  input  b0,
  input  a1,
  input  b1,
  input  a2,
  input  b2,
  input  a3,
  input  b3,
  input  c_in,
  output s0,
  output c_out,
  output s1,
  output s2,
  output s3
);

  wire adder_1_cout, adder_2_cout, adder_3_cout, adder_5_cout, adder_6_cout, adder_7_cout, and_1_out,
       c_out_t, or_1_out, r0, r1, r2, r3;

  Adder #(.width(1)) adder_1 (.a(a0), .b(b0), .out(r0), .cin(c_in), .cout(adder_1_cout));
  Adder #(.width(1)) adder_2 (.a(a1), .b(b1), .out(r1), .cin(adder_1_cout), .cout(adder_2_cout));
  Adder #(.width(1)) adder_3 (.a(a2), .b(b2), .out(r2), .cin(adder_2_cout), .cout(adder_3_cout));
  Adder #(.width(1)) adder_4 (.a(a3), .b(b3), .out(r3), .cin(adder_3_cout), .cout(c_out_t));
  or or_1 (or_1_out, r1, r2);
  Adder #(.width(1)) adder_5 (.a(r0), .b(1'b0), .out(s0), .cout(adder_5_cout));  // open: cin
  Adder #(.width(1)) adder_6 (.a(r1), .b(c_out), .out(s1), .cin(adder_5_cout), .cout(adder_6_cout));
  Adder #(.width(1)) adder_7 (.a(r2), .b(c_out), .out(s2), .cin(adder_6_cout), .cout(adder_7_cout));
  Adder #(.width(1)) adder_8 (.a(r3), .b(1'b0), .out(s3), .cin(adder_7_cout));  // open: cout
  and and_1 (and_1_out, or_1_out, r3);
  or or_2 (c_out, and_1_out, c_out_t);

  // Other names for the same wires on the sheet: c_1 = c_out
endmodule

module somador_12bit_bcd (
  input  a0,
  input  b0,
  input  a1,
  input  b1,
  input  a2,
  input  b2,
  input  a3,
  input  b3,
  input  a0_1,
  input  b0_1,
  input  a1_1,
  input  b1_1,
  input  a2_1,
  input  b2_1,
  input  a3_1,
  input  b3_1,
  input  a0_2,
  input  b0_2,
  input  a1_2,
  input  b1_2,
  input  a2_2,
  input  b2_2,
  input  a3_2,
  input  b3_2,
  output s0,
  output s0_1,
  output s0_2,
  output s1,
  output s1_1,
  output s1_2,
  output s2,
  output s2_1,
  output s2_2,
  output s3,
  output s3_1,
  output s3_2,
  output c_out
);

  wire somador_bcd_1_c_out, somador_bcd_2_c_out;

  somador_bcd somador_bcd_1 (
    .a0(a0), .b0(b0), .a1(a1), .b1(b1), .a2(a2), .b2(b2), .a3(a3), .b3(b3), .c_in(1'b0), .s0(s0),
    .c_out(somador_bcd_1_c_out), .s1(s1), .s2(s2), .s3(s3));
  somador_bcd somador_bcd_2 (
    .a0(a0_1), .b0(b0_1), .a1(a1_1), .b1(b1_1), .a2(a2_1), .b2(b2_1), .a3(a3_1), .b3(b3_1),
    .c_in(somador_bcd_1_c_out), .s0(s0_1), .c_out(somador_bcd_2_c_out), .s1(s1_1), .s2(s2_1), .s3(s3_1));
  somador_bcd somador_bcd_3 (
    .a0(a0_2), .b0(b0_2), .a1(a1_2), .b1(b1_2), .a2(a2_2), .b2(b2_2), .a3(a3_2), .b3(b3_2),
    .c_in(somador_bcd_2_c_out), .s0(s0_2), .c_out(c_out), .s1(s1_2), .s2(s2_2), .s3(s3_2));
endmodule

module registrador_12bit (
  input  a0,
  input  b0,
  input  a1,
  input  b1,
  input  a2,
  input  b2,
  input  a3,
  input  b3,
  input  a0_1,
  input  b0_1,
  input  a1_1,
  input  b1_1,
  input  a2_1,
  input  b2_1,
  input  a3_1,
  input  b3_1,
  input  a0_2,
  input  b0_2,
  input  s,
  input  a1_2,
  input  b1_2,
  input  clock,
  input  a2_2,
  input  b2_2,
  input  r,
  input  a3_2,
  input  b3_2,
  output s0,
  output s0_1,
  output s0_2,
  output s1,
  output s1_1,
  output s1_2,
  output s2,
  output s2_1,
  output s2_2,
  output s3,
  output s3_1,
  output s3_2
);

  registrador registrador_1 (
    .a0(a0), .s0(b0), .a1(a1), .s1(b1), .a2(a2), .s2(b2), .a3(a3), .s3(b3), .s(s), .clock(clock), .r(r),
    .q0(s0), .q1(s1), .q2(s2), .q3(s3));
  registrador registrador_2 (
    .a0(a0_1), .s0(b0_1), .a1(a1_1), .s1(b1_1), .a2(a2_1), .s2(b2_1), .a3(a3_1), .s3(b3_1), .s(s),
    .clock(clock), .r(r), .q0(s0_1), .q1(s1_1), .q2(s2_1), .q3(s3_1));
  registrador registrador_3 (
    .a0(a0_2), .s0(b0_2), .a1(a1_2), .s1(b1_2), .a2(a2_2), .s2(b2_2), .a3(a3_2), .s3(b3_2), .s(s),
    .clock(clock), .r(r), .q0(s0_2), .q1(s1_2), .q2(s2_2), .q3(s3_2));
endmodule

module subtrator_bcd (
  input  a0,
  input  b0,
  input  a1,
  input  b1,
  input  a2,
  input  b2,
  input  a3,
  input  b3,
  input  c_in,
  output s0,
  output c_out,
  output s1,
  output s2,
  output s3
);

  wire rc0, rc1, rc2, rc3;

  somador_bcd somador_bcd_1 (
    .a0(a0), .b0(rc0), .a1(a1), .b1(rc1), .a2(a2), .b2(rc2), .a3(a3), .b3(rc3), .c_in(c_in), .s0(s0),
    .c_out(c_out), .s1(s1), .s2(s2), .s3(s3));
  complemento_9 complemento_9_1 (.a0(b0), .a1(b1), .a2(b2), .a3(b3), .x(rc0), .y(rc1), .z(rc2), .w(rc3));
endmodule

module complemento_9 (
  input  a0,
  input  a1,
  input  a2,
  input  a3,
  output x,
  output y,
  output z,
  output w
);

  wire not_1_out, not_2_out, not_3_out;

  not not_1 (not_1_out, a1);
  not not_2 (not_2_out, a2);
  not not_3 (not_3_out, a3);
  not not_4 (x, a0);
  xor xor_1 (z, a1, a2);
  and and_1 (w, not_1_out, not_2_out, not_3_out);

  assign y = a1;

  // Other names for the same wires on the sheet: r0 = a0; r1 = a1; r2 = a2; r3 = a3
endmodule

module subtrator_bcd_12bit (
  input  a0,
  input  b0,
  input  a1,
  input  b1,
  input  a2,
  input  b2,
  input  a3,
  input  b3,
  input  a0_1,
  input  b0_1,
  input  a1_1,
  input  b1_1,
  input  a2_1,
  input  b2_1,
  input  a3_1,
  input  b3_1,
  input  a0_2,
  input  b0_2,
  input  a1_2,
  input  b1_2,
  input  a2_2,
  input  b2_2,
  input  a3_2,
  input  b3_2,
  output s3,
  output s2,
  output s1,
  output s0,
  output s3_1,
  output s2_1,
  output s1_1,
  output s0_1,
  output s3_2,
  output s2_2,
  output s1_2,
  output s0_2
);

  wire EAC, s0_1_t, s0_2_t, s0_t, s1_1_t, s1_2_t, s1_t, s2_1_t, s2_2_t, s2_t, s3_1_t, s3_2_t, s3_t,
       subtrator_bcd_4bit_1_c_out, subtrator_bcd_4bit_2_c_out;

  subtrator_bcd_4bit subtrator_bcd_4bit_1 (
    .a0(a0), .b0(b0), .a1(a1), .b1(b1), .a2(a2), .b2(b2), .a3(a3), .b3(b3), .s0(s0_t),
    .c_out(subtrator_bcd_4bit_1_c_out), .s1(s1_t), .s2(s2_t), .s3(s3_t));  // open: c_in
  subtator_fix subtator_fix_1 (
    .a0(s0_t), .a1(s1_t), .a2(s2_t), .a3(s3_t), .a0_1(s0_1_t), .a1_1(s1_1_t), .a2_1(s2_1_t), .a3_1(s3_1_t),
    .a0_2(s0_2_t), .a1_2(s1_2_t), .a2_2(s2_2_t), .a3_2(s3_2_t), .EAC(EAC), .s0(s0), .s0_1(s0_1), .s0_2(s0_2),
    .s1(s1), .s1_1(s1_1), .s1_2(s1_2), .s2(s2), .s2_1(s2_1), .s2_2(s2_2), .s3(s3), .s3_1(s3_1), .s3_2(s3_2));
  subtrator_bcd_4bit subtrator_bcd_4bit_2 (
    .a0(a0_1), .b0(b0_1), .a1(a1_1), .b1(b1_1), .a2(a2_1), .b2(b2_1), .a3(a3_1), .b3(b3_1),
    .c_in(subtrator_bcd_4bit_1_c_out), .s0(s0_1_t), .c_out(subtrator_bcd_4bit_2_c_out), .s1(s1_1_t),
    .s2(s2_1_t), .s3(s3_1_t));
  subtrator_bcd_4bit subtrator_bcd_4bit_3 (
    .a0(a0_2), .b0(b0_2), .a1(a1_2), .b1(b1_2), .a2(a2_2), .b2(b2_2), .a3(a3_2), .b3(b3_2),
    .c_in(subtrator_bcd_4bit_2_c_out), .s0(s0_2_t), .c_out(EAC), .s1(s1_2_t), .s2(s2_2_t), .s3(s3_2_t));
endmodule

module subtrator_bcd_4bit (
  input  a0,
  input  b0,
  input  a1,
  input  b1,
  input  a2,
  input  b2,
  input  a3,
  input  b3,
  input  c_in,
  output s0,
  output c_out,
  output s1,
  output s2,
  output s3
);

  wire rc0, rc1, rc2, rc3;

  somador_bcd somador_bcd_1 (
    .a0(a0), .b0(rc0), .a1(a1), .b1(rc1), .a2(a2), .b2(rc2), .a3(a3), .b3(rc3), .c_in(c_in), .s0(s0),
    .c_out(c_out), .s1(s1), .s2(s2), .s3(s3));
  complemento_9 complemento_9_1 (.a0(b0), .a1(b1), .a2(b2), .a3(b3), .x(rc0), .y(rc1), .z(rc2), .w(rc3));
endmodule

module subtator_fix (
  input  a0,
  input  a1,
  input  a2,
  input  a3,
  input  a0_1,
  input  a1_1,
  input  a2_1,
  input  a3_1,
  input  a0_2,
  input  a1_2,
  input  a2_2,
  input  a3_2,
  input  EAC,
  output s0,
  output s0_1,
  output s0_2,
  output s1,
  output s1_1,
  output s1_2,
  output s2,
  output s2_1,
  output s2_2,
  output s3,
  output s3_1,
  output s3_2
);

  wire EAC_t, i0, i1, i2, i3, i4, i5, i6, i7, i8, i9, i10, i11, s0_1_t, s0_2_t, s0_t, s1_1_t, s1_2_t, s1_t,
       s2_1_t, s2_2_t, s2_t, s3_1_t, s3_2_t, s3_t;

  not not_1 (EAC_t, EAC);
  Multiplexer multiplexer_1 (.in0(s0_t), .in1(i0), .out(s0), .sel(EAC_t));
  Multiplexer multiplexer_2 (.in0(s0_2_t), .in1(i8), .out(s0_2), .sel(EAC_t));
  Multiplexer multiplexer_3 (.in0(s1_t), .in1(i1), .out(s1), .sel(EAC_t));
  Multiplexer multiplexer_4 (.in0(s1_2_t), .in1(i9), .out(s1_2), .sel(EAC_t));
  Multiplexer multiplexer_5 (.in0(s2_t), .in1(i2), .out(s2), .sel(EAC_t));
  Multiplexer multiplexer_6 (.in0(s2_2_t), .in1(i10), .out(s2_2), .sel(EAC_t));
  Multiplexer multiplexer_7 (.in0(s3_t), .in1(i3), .out(s3), .sel(EAC_t));
  Multiplexer multiplexer_8 (.in0(s3_2_t), .in1(i11), .out(s3_2), .sel(EAC_t));
  Multiplexer multiplexer_9 (.in0(s0_1_t), .in1(i4), .out(s0_1), .sel(EAC_t));
  Multiplexer multiplexer_10 (.in0(s1_1_t), .in1(i5), .out(s1_1), .sel(EAC_t));
  somador_12bit_bcd somador_12bit_bcd_1 (
    .a0(a0), .b0(1'b1), .a1(a1), .b1(1'b0), .a2(a2), .b2(1'b0), .a3(a3), .b3(1'b0), .a0_1(a0_1), .b0_1(1'b0),
    .a1_1(a1_1), .b1_1(1'b0), .a2_1(a2_1), .b2_1(1'b0), .a3_1(a3_1), .b3_1(1'b0), .a0_2(a0_2), .b0_2(1'b0),
    .a1_2(a1_2), .b1_2(1'b0), .a2_2(a2_2), .b2_2(1'b0), .a3_2(a3_2), .b3_2(1'b0), .s0(s0_t), .s0_1(s0_1_t),
    .s0_2(s0_2_t), .s1(s1_t), .s1_1(s1_1_t), .s1_2(s1_2_t), .s2(s2_t), .s2_1(s2_1_t), .s2_2(s2_2_t),
    .s3(s3_t), .s3_1(s3_1_t), .s3_2(s3_2_t));  // open: c_out
  Multiplexer multiplexer_11 (.in0(s2_1_t), .in1(i6), .out(s2_1), .sel(EAC_t));
  Multiplexer multiplexer_12 (.in0(s3_1_t), .in1(i7), .out(s3_1), .sel(EAC_t));
  complemento_9 complemento_9_1 (.a0(a0), .a1(a1), .a2(a2), .a3(a3), .x(i0), .y(i1), .z(i2), .w(i3));
  complemento_9 complemento_9_2 (.a0(a0_1), .a1(a1_1), .a2(a2_1), .a3(a3_1), .x(i4), .y(i5), .z(i6), .w(i7));
  complemento_9 complemento_9_3 (.a0(a0_2), .a1(a1_2), .a2(a2_2), .a3(a3_2), .x(i8), .y(i9), .z(i10), .w(i11));

  // Other names for the same wires on the sheet: r0 = s0; r0_1 = s0_1; r0_2 = s0_2; r1 = s1; r1_1 = s1_1; r1_2 = s1_2;
  //   r2 = s2; r2_1 = s2_1; r2_2 = s2_2; r3 = s3; r3_1 = s3_1; r3_2 = s3_2
endmodule

module contador (
  input  in_1,
  input  in_2,
  input  in_3,
  input  in_4,
  input  in_5,
  input  in_6,
  input  in_7,
  input  in_8,
  input  in_9,
  input  in_10,
  input  in_11,
  input  in_12,
  input  up_dw,
  input  mx_mi
);

  wire clock, conversor_bcd_sete_segimentos_1_a, conversor_bcd_sete_segimentos_1_b,
       conversor_bcd_sete_segimentos_1_c, conversor_bcd_sete_segimentos_1_d,
       conversor_bcd_sete_segimentos_1_e, conversor_bcd_sete_segimentos_1_f,
       conversor_bcd_sete_segimentos_1_g, conversor_bcd_sete_segimentos_2_a,
       conversor_bcd_sete_segimentos_2_b, conversor_bcd_sete_segimentos_2_c,
       conversor_bcd_sete_segimentos_2_d, conversor_bcd_sete_segimentos_2_e,
       conversor_bcd_sete_segimentos_2_f, conversor_bcd_sete_segimentos_2_g,
       conversor_bcd_sete_segimentos_3_a, conversor_bcd_sete_segimentos_3_b,
       conversor_bcd_sete_segimentos_3_c, conversor_bcd_sete_segimentos_3_d,
       conversor_bcd_sete_segimentos_3_e, conversor_bcd_sete_segimentos_3_f,
       conversor_bcd_sete_segimentos_3_g, conversor_bcd_sete_segimentos_4_a,
       conversor_bcd_sete_segimentos_4_b, conversor_bcd_sete_segimentos_4_c,
       conversor_bcd_sete_segimentos_4_d, conversor_bcd_sete_segimentos_4_e,
       conversor_bcd_sete_segimentos_4_f, conversor_bcd_sete_segimentos_4_g,
       conversor_bcd_sete_segimentos_5_a, conversor_bcd_sete_segimentos_5_b,
       conversor_bcd_sete_segimentos_5_c, conversor_bcd_sete_segimentos_5_d,
       conversor_bcd_sete_segimentos_5_e, conversor_bcd_sete_segimentos_5_f,
       conversor_bcd_sete_segimentos_5_g, conversor_bcd_sete_segimentos_6_a,
       conversor_bcd_sete_segimentos_6_b, conversor_bcd_sete_segimentos_6_c,
       conversor_bcd_sete_segimentos_6_d, conversor_bcd_sete_segimentos_6_e,
       conversor_bcd_sete_segimentos_6_f, conversor_bcd_sete_segimentos_6_g,
       conversor_bcd_sete_segimentos_7_a, conversor_bcd_sete_segimentos_7_b,
       conversor_bcd_sete_segimentos_7_c, conversor_bcd_sete_segimentos_7_d,
       conversor_bcd_sete_segimentos_7_e, conversor_bcd_sete_segimentos_7_f,
       conversor_bcd_sete_segimentos_7_g, conversor_bcd_sete_segimentos_8_a,
       conversor_bcd_sete_segimentos_8_b, conversor_bcd_sete_segimentos_8_c,
       conversor_bcd_sete_segimentos_8_d, conversor_bcd_sete_segimentos_8_e,
       conversor_bcd_sete_segimentos_8_f, conversor_bcd_sete_segimentos_8_g,
       conversor_bcd_sete_segimentos_9_a, conversor_bcd_sete_segimentos_9_b,
       conversor_bcd_sete_segimentos_9_c, conversor_bcd_sete_segimentos_9_d,
       conversor_bcd_sete_segimentos_9_e, conversor_bcd_sete_segimentos_9_f,
       conversor_bcd_sete_segimentos_9_g, load, M0, m0_t, M1, m1_t, M2, m2_t, M3, m3_t, M4, m4_t, M5, m5_t,
       M6, m6_t, M7, m7_t, M8, m8_t, M9, m9_t, M10, m10_t, M11, m11_t, p0, p1, p2, p3, q0, q1, q2, q3, q4,
       q5, q6, q7, q8, q9, q10, q11, S0, s0_t, S1, s1_t, S2, s2_t, S3, s3_t, S4, s4_t, S5, s5_t, S6, s6_t,
       S7, s7_t, S8, s8_t, S9, s9_t, S10, s10_t, S11, s11_t, step, w0, w1, w2, w3, w4, w5, w6, w7, w8, w9,
       w10, w11;

  Clock #(.lowDuration(3)) clock_1 (.out(clock));
  LED CK (.in(clock));
  LED LED_1 ();  // open: in
  conversor_bcd_sete_segimentos conversor_bcd_sete_segimentos_1 (
    .d0(q8), .d1(q9), .d2(q10), .d3(q11), .c(conversor_bcd_sete_segimentos_1_c),
    .d(conversor_bcd_sete_segimentos_1_d), .a(conversor_bcd_sete_segimentos_1_a),
    .b(conversor_bcd_sete_segimentos_1_b), .e(conversor_bcd_sete_segimentos_1_e),
    .f(conversor_bcd_sete_segimentos_1_f), .g(conversor_bcd_sete_segimentos_1_g));
  _7_Segment_Display u_7_segment_display_1 (
    .g(conversor_bcd_sete_segimentos_1_g), .f(conversor_bcd_sete_segimentos_1_f),
    .a(conversor_bcd_sete_segimentos_1_a), .b(conversor_bcd_sete_segimentos_1_b),
    .e(conversor_bcd_sete_segimentos_1_e), .d(conversor_bcd_sete_segimentos_1_d),
    .c(conversor_bcd_sete_segimentos_1_c));  // open: dp
  Button button_step (.out(step));
  Button u_load (.out(load));
  Button #(.press("passive")) clr ();  // open: out
  registrador_12bit Numero_Operacao (
    .a0(w0), .a1(w1), .a2(w2), .a3(w3), .a0_1(w4), .a1_1(w5), .a2_1(w6), .a3_1(w7), .a0_2(w8), .s(1'b0),
    .a1_2(w9), .clock(clock), .a2_2(w10), .r(1'b0), .a3_2(w11), .s0(q0), .s0_1(q4), .s0_2(q8), .s1(q1),
    .s1_1(q5), .s1_2(q9), .s2(q2), .s2_1(q6), .s2_2(q10), .s3(q3), .s3_1(q7), .s3_2(q11));  // open: b0, b1, b2, b3, b0_1, b1_1, b2_1, b3_1, b0_2, b1_2, b2_2, b3_2
  registrador_12bit Numero_Maximo (
    .a0(M0), .b0(in_1), .a1(M1), .b1(in_2), .a2(M2), .b2(in_3), .a3(M3), .b3(in_4), .a0_1(M4), .b0_1(in_5),
    .a1_1(M5), .b1_1(in_6), .a2_1(M6), .b2_1(in_7), .a3_1(M7), .b3_1(in_8), .a0_2(M8), .b0_2(in_9),
    .a1_2(M9), .b1_2(in_10), .clock(clock), .a2_2(M10), .b2_2(in_11), .a3_2(M11), .b3_2(in_12), .s0(M0),
    .s0_1(M4), .s0_2(M8), .s1(M1), .s1_1(M5), .s1_2(M9), .s2(M2), .s2_1(M6), .s2_2(M10), .s3(M3), .s3_1(M7),
    .s3_2(M11));  // open: s, r
  registrador_12bit Numero_Minimo (
    .a0(m0_t), .b0(in_1), .a1(m1_t), .b1(in_2), .a2(m2_t), .b2(in_3), .a3(m3_t), .b3(in_4), .a0_1(m4_t),
    .b0_1(in_5), .a1_1(m5_t), .b1_1(in_6), .a2_1(m6_t), .b2_1(in_7), .a3_1(m7_t), .b3_1(in_8), .a0_2(m8_t),
    .b0_2(in_9), .a1_2(m9_t), .b1_2(in_10), .clock(clock), .a2_2(m10_t), .b2_2(in_11), .a3_2(m11_t),
    .b3_2(in_12), .s0(m0_t), .s0_1(m4_t), .s0_2(m8_t), .s1(m1_t), .s1_1(m5_t), .s1_2(m9_t), .s2(m2_t),
    .s2_1(m6_t), .s2_2(m10_t), .s3(m3_t), .s3_1(m7_t), .s3_2(m11_t));  // open: s, r
  conversor_bcd_sete_segimentos conversor_bcd_sete_segimentos_2 (
    .d0(q4), .d1(q5), .d2(q6), .d3(q7), .c(conversor_bcd_sete_segimentos_2_c),
    .d(conversor_bcd_sete_segimentos_2_d), .a(conversor_bcd_sete_segimentos_2_a),
    .b(conversor_bcd_sete_segimentos_2_b), .e(conversor_bcd_sete_segimentos_2_e),
    .f(conversor_bcd_sete_segimentos_2_f), .g(conversor_bcd_sete_segimentos_2_g));
  _7_Segment_Display u_7_segment_display_2 (
    .g(conversor_bcd_sete_segimentos_2_g), .f(conversor_bcd_sete_segimentos_2_f),
    .a(conversor_bcd_sete_segimentos_2_a), .b(conversor_bcd_sete_segimentos_2_b),
    .e(conversor_bcd_sete_segimentos_2_e), .d(conversor_bcd_sete_segimentos_2_d),
    .c(conversor_bcd_sete_segimentos_2_c));  // open: dp
  Multiplexer multiplexer_1 (.in0(s0_t), .in1(S0), .out(w0), .sel(up_dw));
  Multiplexer multiplexer_2 (.in0(s4_t), .in1(S4), .out(w4), .sel(up_dw));
  Multiplexer multiplexer_3 (.in0(s8_t), .in1(S8), .out(w8), .sel(up_dw));
  Multiplexer multiplexer_4 (.in0(s1_t), .in1(S1), .out(w1), .sel(up_dw));
  Multiplexer multiplexer_5 (.in0(s5_t), .in1(S5), .out(w5), .sel(up_dw));
  Multiplexer multiplexer_6 (.in0(s9_t), .in1(S9), .out(w9), .sel(up_dw));
  Multiplexer multiplexer_7 (.in0(s2_t), .in1(S2), .out(w2), .sel(up_dw));
  Multiplexer multiplexer_8 (.in0(s6_t), .in1(S6), .out(w6), .sel(up_dw));
  Multiplexer multiplexer_9 (.in0(s10_t), .in1(S10), .out(w10), .sel(up_dw));
  registrador u_Step (
    .s0(in_1), .s1(in_2), .s2(in_3), .s3(in_4), .s(step), .clock(clock), .q0(p0), .q1(p1), .q2(p2), .q3(p3));  // open: a0, a1, a2, a3, r
  conversor_bcd_sete_segimentos conversor_bcd_sete_segimentos_3 (
    .d0(q0), .d1(q1), .d2(q2), .d3(q3), .c(conversor_bcd_sete_segimentos_3_c),
    .d(conversor_bcd_sete_segimentos_3_d), .a(conversor_bcd_sete_segimentos_3_a),
    .b(conversor_bcd_sete_segimentos_3_b), .e(conversor_bcd_sete_segimentos_3_e),
    .f(conversor_bcd_sete_segimentos_3_f), .g(conversor_bcd_sete_segimentos_3_g));
  Multiplexer multiplexer_10 (.in0(s3_t), .in1(S3), .out(w3), .sel(up_dw));
  Multiplexer multiplexer_11 (.in0(s7_t), .in1(S7), .out(w7), .sel(up_dw));
  Multiplexer multiplexer_12 (.in0(s11_t), .in1(S11), .out(w11), .sel(up_dw));
  _7_Segment_Display u_7_segment_display_3 (
    .g(conversor_bcd_sete_segimentos_3_g), .f(conversor_bcd_sete_segimentos_3_f),
    .a(conversor_bcd_sete_segimentos_3_a), .b(conversor_bcd_sete_segimentos_3_b),
    .e(conversor_bcd_sete_segimentos_3_e), .d(conversor_bcd_sete_segimentos_3_d),
    .c(conversor_bcd_sete_segimentos_3_c));  // open: dp
  subtrator_bcd_12bit Subtrator_12bits (
    .a0(q0), .b0(p0), .a1(q1), .b1(p1), .a2(q2), .b2(p2), .a3(q3), .b3(p3), .a0_1(q4), .b0_1(1'b0),
    .a1_1(q5), .b1_1(1'b0), .a2_1(q6), .b2_1(1'b0), .a3_1(q7), .b3_1(1'b0), .a0_2(q8), .b0_2(1'b0),
    .a1_2(q9), .b1_2(1'b0), .a2_2(q10), .b2_2(1'b0), .a3_2(q11), .b3_2(1'b0), .s3(s3_t), .s2(s2_t),
    .s1(s1_t), .s0(s0_t), .s3_1(s7_t), .s2_1(s6_t), .s1_1(s5_t), .s0_1(s4_t), .s3_2(s11_t), .s2_2(s10_t),
    .s1_2(s9_t), .s0_2(s8_t));
  somador_12bit_bcd Somador_12bits (
    .a0(q0), .b0(p0), .a1(q1), .b1(p1), .a2(q2), .b2(p2), .a3(q3), .b3(p3), .a0_1(q4), .b0_1(1'b0),
    .a1_1(q5), .b1_1(1'b0), .a2_1(q6), .b2_1(1'b0), .a3_1(q7), .b3_1(1'b0), .a0_2(q8), .b0_2(1'b0),
    .a1_2(q9), .b1_2(1'b0), .a2_2(q10), .b2_2(1'b0), .a3_2(q11), .b3_2(1'b0), .s0(S0), .s0_1(S4), .s0_2(S8),
    .s1(S1), .s1_1(S5), .s1_2(S9), .s2(S2), .s2_1(S6), .s2_2(S10), .s3(S3), .s3_1(S7), .s3_2(S11));  // open: c_out
  conversor_bcd_sete_segimentos conversor_bcd_sete_segimentos_4 (
    .d0(s8_t), .d1(s9_t), .d2(s10_t), .d3(s11_t), .c(conversor_bcd_sete_segimentos_4_c),
    .d(conversor_bcd_sete_segimentos_4_d), .a(conversor_bcd_sete_segimentos_4_a),
    .b(conversor_bcd_sete_segimentos_4_b), .e(conversor_bcd_sete_segimentos_4_e),
    .f(conversor_bcd_sete_segimentos_4_f), .g(conversor_bcd_sete_segimentos_4_g));
  conversor_bcd_sete_segimentos conversor_bcd_sete_segimentos_5 (
    .d0(S8), .d1(S9), .d2(S10), .d3(S11), .c(conversor_bcd_sete_segimentos_5_c),
    .d(conversor_bcd_sete_segimentos_5_d), .a(conversor_bcd_sete_segimentos_5_a),
    .b(conversor_bcd_sete_segimentos_5_b), .e(conversor_bcd_sete_segimentos_5_e),
    .f(conversor_bcd_sete_segimentos_5_f), .g(conversor_bcd_sete_segimentos_5_g));
  _7_Segment_Display u_7_segment_display_4 (
    .g(conversor_bcd_sete_segimentos_4_g), .f(conversor_bcd_sete_segimentos_4_f),
    .a(conversor_bcd_sete_segimentos_4_a), .b(conversor_bcd_sete_segimentos_4_b),
    .e(conversor_bcd_sete_segimentos_4_e), .d(conversor_bcd_sete_segimentos_4_d),
    .c(conversor_bcd_sete_segimentos_4_c));  // open: dp
  _7_Segment_Display u_7_segment_display_5 (
    .g(conversor_bcd_sete_segimentos_5_g), .f(conversor_bcd_sete_segimentos_5_f),
    .a(conversor_bcd_sete_segimentos_5_a), .b(conversor_bcd_sete_segimentos_5_b),
    .e(conversor_bcd_sete_segimentos_5_e), .d(conversor_bcd_sete_segimentos_5_d),
    .c(conversor_bcd_sete_segimentos_5_c));  // open: dp
  conversor_bcd_sete_segimentos conversor_bcd_sete_segimentos_6 (
    .d0(s4_t), .d1(s5_t), .d2(s6_t), .d3(s7_t), .c(conversor_bcd_sete_segimentos_6_c),
    .d(conversor_bcd_sete_segimentos_6_d), .a(conversor_bcd_sete_segimentos_6_a),
    .b(conversor_bcd_sete_segimentos_6_b), .e(conversor_bcd_sete_segimentos_6_e),
    .f(conversor_bcd_sete_segimentos_6_f), .g(conversor_bcd_sete_segimentos_6_g));
  conversor_bcd_sete_segimentos conversor_bcd_sete_segimentos_7 (
    .d0(S4), .d1(S5), .d2(S6), .d3(S7), .c(conversor_bcd_sete_segimentos_7_c),
    .d(conversor_bcd_sete_segimentos_7_d), .a(conversor_bcd_sete_segimentos_7_a),
    .b(conversor_bcd_sete_segimentos_7_b), .e(conversor_bcd_sete_segimentos_7_e),
    .f(conversor_bcd_sete_segimentos_7_f), .g(conversor_bcd_sete_segimentos_7_g));
  _7_Segment_Display u_7_segment_display_6 (
    .g(conversor_bcd_sete_segimentos_6_g), .f(conversor_bcd_sete_segimentos_6_f),
    .a(conversor_bcd_sete_segimentos_6_a), .b(conversor_bcd_sete_segimentos_6_b),
    .e(conversor_bcd_sete_segimentos_6_e), .d(conversor_bcd_sete_segimentos_6_d),
    .c(conversor_bcd_sete_segimentos_6_c));  // open: dp
  _7_Segment_Display u_7_segment_display_7 (
    .g(conversor_bcd_sete_segimentos_7_g), .f(conversor_bcd_sete_segimentos_7_f),
    .a(conversor_bcd_sete_segimentos_7_a), .b(conversor_bcd_sete_segimentos_7_b),
    .e(conversor_bcd_sete_segimentos_7_e), .d(conversor_bcd_sete_segimentos_7_d),
    .c(conversor_bcd_sete_segimentos_7_c));  // open: dp
  conversor_bcd_sete_segimentos conversor_bcd_sete_segimentos_8 (
    .d0(s0_t), .d1(s1_t), .d2(s2_t), .d3(s3_t), .c(conversor_bcd_sete_segimentos_8_c),
    .d(conversor_bcd_sete_segimentos_8_d), .a(conversor_bcd_sete_segimentos_8_a),
    .b(conversor_bcd_sete_segimentos_8_b), .e(conversor_bcd_sete_segimentos_8_e),
    .f(conversor_bcd_sete_segimentos_8_f), .g(conversor_bcd_sete_segimentos_8_g));
  conversor_bcd_sete_segimentos conversor_bcd_sete_segimentos_9 (
    .d0(S0), .d1(S1), .d2(S2), .d3(S3), .c(conversor_bcd_sete_segimentos_9_c),
    .d(conversor_bcd_sete_segimentos_9_d), .a(conversor_bcd_sete_segimentos_9_a),
    .b(conversor_bcd_sete_segimentos_9_b), .e(conversor_bcd_sete_segimentos_9_e),
    .f(conversor_bcd_sete_segimentos_9_f), .g(conversor_bcd_sete_segimentos_9_g));
  _7_Segment_Display u_7_segment_display_8 (
    .g(conversor_bcd_sete_segimentos_8_g), .f(conversor_bcd_sete_segimentos_8_f),
    .a(conversor_bcd_sete_segimentos_8_a), .b(conversor_bcd_sete_segimentos_8_b),
    .e(conversor_bcd_sete_segimentos_8_e), .d(conversor_bcd_sete_segimentos_8_d),
    .c(conversor_bcd_sete_segimentos_8_c));  // open: dp
  _7_Segment_Display u_7_segment_display_9 (
    .g(conversor_bcd_sete_segimentos_9_g), .f(conversor_bcd_sete_segimentos_9_f),
    .a(conversor_bcd_sete_segimentos_9_a), .b(conversor_bcd_sete_segimentos_9_b),
    .e(conversor_bcd_sete_segimentos_9_e), .d(conversor_bcd_sete_segimentos_9_d),
    .c(conversor_bcd_sete_segimentos_9_c));  // open: dp

  // Other names for the same wires on the sheet: a0 = in_1; a1 = in_2; a2 = in_3; a3 = in_4; a4 = in_5; a5 = in_6;
  //   a6 = in_7; a7 = in_8; a8 = in_9; a9 = in_10; a10 = in_11; a11 = in_12

  // Notes on the sheet:
  //   Entradas SW[11:0]
endmodule
