// Logisim project Botão Síncrono.circ as structural Verilog: 1 circuit, main circuit main
module main (
  input  in_1,
  output out_2
);

  wire and_1_out, and_2_out, clock, E1, n0, n1, not_1_out, not_2_out;

  Register #(.width(1)) register_1 (.D(n1), .Q(E1), .clk(clock));  // open: en, clr
  Clock clock_1 (.out(clock));
  not not_1 (not_1_out, E1);
  not not_2 (not_2_out, E1);
  and and_1 (and_1_out, E1, in_1);
  and and_2 (and_2_out, out_2, in_1);
  and and_3 (n0, not_1_out, not_2_out, in_1);
  Register #(.width(1)) register_2 (.D(n0), .Q(out_2), .clk(clock));  // open: en, clr
  or or_1 (n1, and_1_out, and_2_out);

  // Other names for the same wires on the sheet: b0 = out_2; E0 = out_2; bi = in_1
endmodule
