// Logisim project 1.circ as structural Verilog
module Registrado_16_13 (
  input  [3:0] count,
  input  ck,
  input  WRITE,
  input  [12:0] w_data,
  input  clear,
  input  READ,
  input  enable,
  output [12:0] r_data
);

  wire e1, e2, e3, e4, e5, e6, e7, e8, e9, e10, e11, e12, e13, e14, e15, e16;
  wire [12:0] multiplexer_1_out, multiplexer_3_out, multiplexer_4_out, multiplexer_5_out, multiplexer_6_out,
       multiplexer_7_out, multiplexer_8_out, multiplexer_9_out, multiplexer_10_out, multiplexer_11_out,
       multiplexer_12_out, multiplexer_13_out, multiplexer_14_out, multiplexer_15_out, multiplexer_16_out,
       multiplexer_17_out, multiplexer_18_out, r0, r1, r2, r3, r4, r5, r6, r7, r8, r9, r10, r11, r12, r13,
       r14, r15;

  Multiplexer #(.select(4), .width(13)) multiplexer_1 (
    .in0(r0), .in1(r1), .in2(r2), .in3(r3), .in4(r4), .in5(r5), .in6(r6), .in7(r7), .in8(r8), .in9(r9),
    .in10(r10), .in11(r11), .in12(r12), .in13(r13), .in14(r14), .in15(r15), .out(multiplexer_1_out),
    .sel(count));
  LOGICA_DECODER logica_decoder_1 (
    .cmd(count), .enable(enable), .e1(e1), .e2(e2), .e3(e3), .e4(e4), .e5(e5), .e6(e6), .e7(e7), .e8(e8),
    .e9(e9), .e10(e10), .e11(e11), .e12(e12), .e13(e13), .e14(e14), .e15(e15), .e16(e16));
  Multiplexer #(.width(13)) multiplexer_2 (.in0({13{1'b0}}), .in1(multiplexer_1_out), .out(r_data), .sel(READ));
  Multiplexer #(.width(13)) multiplexer_3 (.in0(r0), .in1(w_data), .out(multiplexer_3_out), .sel(e1));
  Register #(.width(13)) register_1 (.D(multiplexer_3_out), .en(WRITE), .clk(ck), .Q(r0), .clr(clear));
  Multiplexer #(.width(13)) multiplexer_4 (.in0(r4), .in1(w_data), .out(multiplexer_4_out), .sel(e5));
  Register #(.width(13)) register_2 (.D(multiplexer_4_out), .en(WRITE), .clk(ck), .Q(r4), .clr(clear));
  Multiplexer #(.width(13)) multiplexer_5 (.in0(r8), .in1(w_data), .out(multiplexer_5_out), .sel(e9));
  Register #(.width(13)) register_3 (.D(multiplexer_5_out), .en(WRITE), .clk(ck), .Q(r8), .clr(clear));
  Multiplexer #(.width(13)) multiplexer_6 (.in0(r12), .in1(w_data), .out(multiplexer_6_out), .sel(e13));
  Register #(.width(13)) register_4 (.D(multiplexer_6_out), .en(WRITE), .clk(ck), .Q(r12), .clr(clear));
  Multiplexer #(.width(13)) multiplexer_7 (.in0(r1), .in1(w_data), .out(multiplexer_7_out), .sel(e2));
  Register #(.width(13)) register_5 (.D(multiplexer_7_out), .en(WRITE), .clk(ck), .Q(r1), .clr(clear));
  Multiplexer #(.width(13)) multiplexer_8 (.in0(r5), .in1(w_data), .out(multiplexer_8_out), .sel(e6));
  Register #(.width(13)) register_6 (.D(multiplexer_8_out), .en(WRITE), .clk(ck), .Q(r5), .clr(clear));
  Multiplexer #(.width(13)) multiplexer_9 (.in0(r9), .in1(w_data), .out(multiplexer_9_out), .sel(e10));
  Register #(.width(13)) register_7 (.D(multiplexer_9_out), .en(WRITE), .clk(ck), .Q(r9), .clr(clear));
  Multiplexer #(.width(13)) multiplexer_10 (.in0(r13), .in1(w_data), .out(multiplexer_10_out), .sel(e14));
  Register #(.width(13)) register_8 (.D(multiplexer_10_out), .en(WRITE), .clk(ck), .Q(r13), .clr(clear));
  Multiplexer #(.width(13)) multiplexer_11 (.in0(r2), .in1(w_data), .out(multiplexer_11_out), .sel(e3));
  Register #(.width(13)) register_9 (.D(multiplexer_11_out), .en(WRITE), .clk(ck), .Q(r2), .clr(clear));
  Multiplexer #(.width(13)) multiplexer_12 (.in0(r6), .in1(w_data), .out(multiplexer_12_out), .sel(e7));
  Register #(.width(13)) register_10 (.D(multiplexer_12_out), .en(WRITE), .clk(ck), .Q(r6), .clr(clear));
  Multiplexer #(.width(13)) multiplexer_13 (.in0(r10), .in1(w_data), .out(multiplexer_13_out), .sel(e11));
  Register #(.width(13)) register_11 (.D(multiplexer_13_out), .en(WRITE), .clk(ck), .Q(r10), .clr(clear));
  Multiplexer #(.width(13)) multiplexer_14 (.in0(r14), .in1(w_data), .out(multiplexer_14_out), .sel(e15));
  Register #(.width(13)) register_12 (.D(multiplexer_14_out), .en(WRITE), .clk(ck), .Q(r14), .clr(clear));
  Multiplexer #(.width(13)) multiplexer_15 (.in0(r3), .in1(w_data), .out(multiplexer_15_out), .sel(e4));
  Register #(.width(13)) register_13 (.D(multiplexer_15_out), .en(WRITE), .clk(ck), .Q(r3), .clr(clear));
  Multiplexer #(.width(13)) multiplexer_16 (.in0(r7), .in1(w_data), .out(multiplexer_16_out), .sel(e8));
  Register #(.width(13)) register_14 (.D(multiplexer_16_out), .en(WRITE), .clk(ck), .Q(r7), .clr(clear));
  Multiplexer #(.width(13)) multiplexer_17 (.in0(r11), .in1(w_data), .out(multiplexer_17_out), .sel(e12));
  Register #(.width(13)) register_15 (.D(multiplexer_17_out), .en(WRITE), .clk(ck), .Q(r11), .clr(clear));
  Multiplexer #(.width(13)) multiplexer_18 (.in0(r15), .in1(w_data), .out(multiplexer_18_out), .sel(e16));
  Register #(.width(13)) register_16 (.D(multiplexer_18_out), .en(WRITE), .clk(ck), .Q(r15), .clr(clear));

  // Other names for the same wires on the sheet: c_reg[12:0] = r_data; r = clear; w_d[12:0] = w_data; w_E = WRITE;
  //   w_R = READ

  // Notes on the sheet:
  //   MUX
  //   ENTRADAS
  //   SAIDA
  //   DECODER
endmodule

module decoder_16_13 (
  input  [3:0] cmd,
  input  enable,
  output e1,
  output e2,
  output e3,
  output e4,
  output e5,
  output e6,
  output e7,
  output e8,
  output e9,
  output e10,
  output e11,
  output e12,
  output e13,
  output e14,
  output e15,
  output e16
);

  Decoder #(.select(4)) decoder_1 (
    .out0(e1), .out1(e2), .out2(e3), .out3(e4), .out4(e5), .out5(e6), .out6(e7), .out7(e8), .out8(e9),
    .out9(e10), .out10(e11), .out11(e12), .out12(e13), .out13(e14), .out14(e15), .out15(e16), .sel(cmd),
    .en(enable));
endmodule

module LOGICA_DECODER (
  input  [3:0] cmd,
  input  enable,
  output e1,
  output e2,
  output e3,
  output e4,
  output e5,
  output e6,
  output e7,
  output e8,
  output e9,
  output e10,
  output e11,
  output e12,
  output e13,
  output e14,
  output e15,
  output e16
);

  wire c1_b, c2_b, c3_b, c4_b;

  not not_1 (c1_b, cmd[3]);
  not not_2 (c2_b, cmd[2]);
  not not_3 (c3_b, cmd[1]);
  not not_4 (c4_b, cmd[0]);
  and and_1 (e1, c1_b, c2_b, c3_b, c4_b, enable);
  and and_2 (e2, c1_b, c2_b, c3_b, cmd[0], enable);
  and and_3 (e3, c1_b, c2_b, cmd[1], c4_b, enable);
  and and_4 (e4, c1_b, c2_b, cmd[1], cmd[0], enable);
  and and_5 (e5, c1_b, cmd[2], c3_b, c4_b, enable);
  and and_6 (e6, c1_b, cmd[2], c3_b, cmd[0], enable);
  and and_7 (e7, c1_b, cmd[2], cmd[1], c4_b, enable);
  and and_8 (e8, c1_b, cmd[2], cmd[1], cmd[0], enable);
  and and_9 (e9, cmd[3], c2_b, c3_b, c4_b, enable);
  and and_10 (e10, cmd[3], c2_b, c3_b, cmd[0], enable);
  and and_11 (e11, cmd[3], c2_b, cmd[1], c4_b, enable);
  and and_12 (e12, cmd[3], c2_b, cmd[1], cmd[0], enable);
  and and_13 (e13, cmd[3], cmd[2], c3_b, enable);
  and and_14 (e14, cmd[3], cmd[2], c3_b, cmd[0], enable);
  and and_15 (e15, cmd[3], cmd[2], cmd[1], enable);
  and and_16 (e16, cmd[3], cmd[2], cmd[1], cmd[0], enable);
endmodule

module datapatch (
  input  ck,
  input  [12:0] w_data,
  input  clr_reg,
  input  w_reg,
  input  r_reg,
  input  s_in,
  output comp,
  output [12:0] r_data
);

  wire or_1_out;
  wire [3:0] c_dt, count, index, pass;

  Multiplexer #(.width(4)) multiplexer_1 (.in0(4'b0001), .in1(4'b1111), .out(pass), .sel(s_in));
  Multiplexer #(.width(4)) multiplexer_2 (.in0(count), .in1(c_dt), .out(index), .sel(s_in));
  or or_1 (or_1_out, r_reg, w_reg);
  Register #(.width(4)) u_count (.D(c_dt), .en(or_1_out), .clk(ck), .Q(count), .clr(clr_reg));
  Adder #(.width(4)) adder_1 (.a(pass), .b(count), .out(c_dt));  // open: cin, cout
  comp_zero comp_zero_1 (.co_in(count), .co_out(comp));
  registradores registradores_1 (
    .count(index), .ck(ck), .WRITE(w_reg), .w_data(w_data), .clear(clr_reg), .READ(r_reg), .r_data(r_data));

  // Notes on the sheet:
  //   MULTIPLEXADORES
  //   ENTRADAS
  //   CONSTANTES
  //   SOMADOR
  //   COMPARADOR COM ZERO
  //   REGISTRADOR_16BITx13
  //   SAIDAS
endmodule

module comp_zero (
  input  [3:0] co_in,
  output co_out
);

  wire or_1_out, or_2_out, or_3_out;

  or or_1 (or_1_out, co_in[0], co_in[1]);
  or or_2 (or_2_out, or_1_out, co_in[2]);
  or or_3 (or_3_out, or_2_out, co_in[3]);
  not not_1 (co_out, or_3_out);

  // Notes on the sheet:
  //   COMPARADOR COM ZERO
endmodule

module bloco_controle (
  input  ck,
  input  wr,
  input  rd,
  input  clr_info,
  input  comp,
  output s_in,
  output clr_reg,
  output w_reg,
  output r_reg,
  output fu,
  output em
);

  wire [1:0] last_state, state;

  Register #(.width(2)) u_state (.D(state), .en(1'b1), .clk(ck), .Q(last_state), .clr(1'b0));
  logica_de_controle logica_de_controle_1 (
    .last_state(last_state), .wr(wr), .rd(rd), .clr_lifo(clr_info), .comp(comp), .state(state), .S_in(s_in),
    .clr_reg(clr_reg), .w_reg(w_reg), .r_reg(r_reg), .fu(fu), .em(em));

  // Notes on the sheet:
  //   BLOCO DE CONTROLE
  //   SAIDAS
endmodule

module logica_de_controle (
  input  [1:0] last_state,
  input  wr,
  input  rd,
  input  clr_lifo,
  input  comp,
  output [1:0] state,
  output S_in,
  output clr_reg,
  output w_reg,
  output r_reg,
  output fu,
  output em
);

  wire and_1_out, and_2_out, and_3_out, and_4_out, and_10_out, and_11_out, not_1_out, not_2_out, not_3_out,
       not_4_out;

  not not_1 (not_1_out, last_state[1]);
  not not_2 (not_2_out, last_state[0]);
  not not_3 (not_3_out, wr);
  not not_4 (not_4_out, clr_lifo);
  and and_1 (and_1_out, not_1_out, not_2_out, clr_lifo);
  and and_2 (and_2_out, not_1_out, not_2_out, not_3_out, rd);
  and and_3 (and_3_out, not_1_out, not_2_out, clr_lifo);
  and and_4 (and_4_out, not_1_out, not_2_out, wr);
  and and_5 (S_in, not_1_out, not_2_out, not_3_out, rd, not_4_out);
  and and_6 (clr_reg, not_1_out, not_2_out, clr_lifo);
  and and_7 (w_reg, not_1_out, not_2_out, wr, not_4_out);
  and and_8 (r_reg, not_1_out, not_2_out, not_3_out, rd, not_4_out);
  and and_9 (fu, not_1_out, last_state[0], comp);
  and and_10 (and_10_out, last_state[1], comp);
  and and_11 (and_11_out, last_state[1], last_state[0]);
  or or_1 (state[1], and_1_out, and_2_out);
  or or_2 (state[0], and_3_out, and_4_out);
  or or_3 (em, and_10_out, and_11_out);
endmodule

module LIFO (
  input  clr_info,
  input  wr,
  input  rd,
  input  ck,
  input  [12:0] w_data,
  output [12:0] r_data,
  output fu,
  output em
);

  wire clr_reg, comp, r_reg, s_in, w_reg;

  bloco_controle bloco_controle_1 (
    .ck(ck), .wr(wr), .rd(rd), .clr_info(clr_info), .comp(comp), .s_in(s_in), .clr_reg(clr_reg),
    .w_reg(w_reg), .r_reg(r_reg), .fu(fu), .em(em));
  datapatch datapatch_1 (
    .ck(ck), .w_data(w_data), .clr_reg(clr_reg), .w_reg(w_reg), .r_reg(s_in), .s_in(r_reg), .comp(comp),
    .r_data(r_data));

  // Notes on the sheet:
  //   ENTRADAS
  //   BLOCO DE CONTROLE
  //   DATAPATCH
  //   SAIDAS
endmodule

module LIFO_INTERFACE (
);

  wire ck, clr_info, em, fu, rd, wr;
  wire [12:0] r_data, w_data;

  Button u_wr (.out(wr));
  Button u_rd (.out(rd));
  Button u_clr_info (.out(clr_info));
  DipSwitch #(.number(13)) dipswitch_1 (
    .sw1(w_data[12]), .sw2(w_data[11]), .sw3(w_data[10]), .sw4(w_data[9]), .sw5(w_data[8]), .sw6(w_data[7]),
    .sw7(w_data[6]), .sw8(w_data[5]), .sw9(w_data[4]), .sw10(w_data[3]), .sw11(w_data[2]), .sw12(w_data[1]),
    .sw13(w_data[0]));
  Clock clock_1 (.out(ck));
  LIFO lifo_1 (.clr_info(clr_info), .wr(wr), .rd(rd), .ck(ck), .w_data(w_data), .r_data(r_data), .fu(fu), .em(em));
  _7_Segment_Display u_7_segment_display_1 ();  // open: g, f, a, b, e, d, c, dp
  // BCD_to_7_Segment_decoder bcd_to_7_segment_decoder_1: pin names not known
  // Binary_to_BCD_converter #(.binvalue(13)) binary_to_bcd_converter_1: pin names not known; wires that end beside it: r_data
  _7_Segment_Display u_7_segment_display_2 ();  // open: g, f, a, b, e, d, c, dp
  // BCD_to_7_Segment_decoder bcd_to_7_segment_decoder_2: pin names not known
  _7_Segment_Display u_7_segment_display_3 ();  // open: g, f, a, b, e, d, c, dp
  _7_Segment_Display u_7_segment_display_4 ();  // open: g, f, a, b, e, d, c, dp
  // BCD_to_7_Segment_decoder bcd_to_7_segment_decoder_3: pin names not known
  // BCD_to_7_Segment_decoder bcd_to_7_segment_decoder_4: pin names not known
  LED u_fu (.in(fu));
  LED u_em (.in(em));

  // Notes on the sheet:
  //   ENTRADAS + CLOCK
  //   CIRCUITO DA LIFO
  //   SAIDAS : BIN-BCD + BCD-7_SEGUIMENTOS
endmodule

module LOGICA_DECODER2 (
  input  [3:0] cmd,
  input  enable,
  output e1,
  output e2,
  output e3,
  output e4,
  output e5,
  output e6,
  output e7,
  output e8,
  output e9,
  output e10,
  output e11,
  output e12,
  output e13,
  output e14,
  output e15,
  output e16
);

  wire not_1_out, not_2_out, not_3_out, not_4_out;

  not not_1 (not_1_out, cmd[3]);
  not not_2 (not_2_out, cmd[2]);
  not not_3 (not_3_out, cmd[1]);
  not not_4 (not_4_out, cmd[0]);
  and and_1 (e1, not_1_out, not_2_out, not_3_out, not_4_out, enable);
  and and_2 (e2, not_1_out, not_2_out, not_3_out, cmd[0], enable);
  and and_3 (e3, not_1_out, not_2_out, cmd[1], not_4_out, enable);
  and and_4 (e4, not_1_out, not_2_out, cmd[1], cmd[0], enable);
  and and_5 (e5, not_1_out, cmd[2], not_3_out, not_4_out, enable);
  and and_6 (e6, not_1_out, cmd[2], not_3_out, cmd[0], enable);
  and and_7 (e7, not_1_out, cmd[2], cmd[1], not_4_out, enable);
  and and_8 (e8, not_1_out, cmd[2], cmd[1], cmd[0], enable);
  and and_9 (e9, cmd[3], not_2_out, not_3_out, not_4_out, enable);
  and and_10 (e10, cmd[3], not_2_out, not_3_out, cmd[0], enable);
  and and_11 (e11, cmd[3], not_2_out, cmd[1], not_4_out, enable);
  and and_12 (e12, cmd[3], not_2_out, cmd[1], cmd[0], enable);
  and and_13 (e13, cmd[3], cmd[2], not_3_out, enable);
  and and_14 (e14, cmd[3], cmd[2], not_3_out, cmd[0], enable);
  and and_15 (e15, cmd[3], cmd[2], cmd[1], enable);
  and and_16 (e16, cmd[3], cmd[2], cmd[1], cmd[0], enable);
endmodule

module registradores (
  input  [3:0] count,
  input  ck,
  input  WRITE,
  input  [12:0] w_data,
  input  clear,
  input  READ,
  output [12:0] r_data
);

  wire e1, e2, e3, e4, e5, e6, e7, e8, e9, e10, e11, e12, e13, e14, e15, e16;
  wire [12:0] multiplexer_1_out, r0, r1, r2, r3, r4, r5, r6, r7, r8, r9, r10, r11, r12, r13, r14, r15;

  Multiplexer #(.select(4), .width(13)) multiplexer_1 (
    .in0(r0), .in1(r1), .in2(r2), .in3(r3), .in4(r4), .in5(r5), .in6(r6), .in7(r7), .in8(r8), .in9(r9),
    .in10(r10), .in11(r11), .in12(r12), .in13(r13), .in14(r14), .in15(r15), .out(multiplexer_1_out),
    .sel(count));
  LOGICA_DECODER logica_decoder_1 (
    .cmd(count), .enable(WRITE), .e1(e1), .e2(e2), .e3(e3), .e4(e4), .e5(e5), .e6(e6), .e7(e7), .e8(e8),
    .e9(e9), .e10(e10), .e11(e11), .e12(e12), .e13(e13), .e14(e14), .e15(e15), .e16(e16));
  Multiplexer #(.width(13)) multiplexer_2 (.in0({13{1'b0}}), .in1(multiplexer_1_out), .out(r_data), .sel(READ));
  Register #(.width(13)) register_1 (.D(w_data), .en(e1), .clk(ck), .Q(r0), .clr(clear));
  Register #(.width(13)) register_2 (.D(w_data), .en(e5), .clk(ck), .Q(r4), .clr(clear));
  Register #(.width(13)) register_3 (.D(w_data), .en(e9), .clk(ck), .Q(r8), .clr(clear));
  Register #(.width(13)) register_4 (.D(w_data), .en(e13), .clk(ck), .Q(r12), .clr(clear));
  Register #(.width(13)) register_5 (.D(w_data), .en(e2), .clk(ck), .Q(r1), .clr(clear));
  Register #(.width(13)) register_6 (.D(w_data), .en(e6), .clk(ck), .Q(r5), .clr(clear));
  Register #(.width(13)) register_7 (.D(w_data), .en(e10), .clk(ck), .Q(r9), .clr(clear));
  Register #(.width(13)) register_8 (.D(w_data), .en(e14), .clk(ck), .Q(r13), .clr(clear));
  Register #(.width(13)) register_9 (.D(w_data), .en(e3), .clk(ck), .Q(r2), .clr(clear));
  Register #(.width(13)) register_10 (.D(w_data), .en(e7), .clk(ck), .Q(r6), .clr(clear));
  Register #(.width(13)) register_11 (.D(w_data), .en(e11), .clk(ck), .Q(r10), .clr(clear));
  Register #(.width(13)) register_12 (.D(w_data), .en(e15), .clk(ck), .Q(r14), .clr(clear));
  Register #(.width(13)) register_13 (.D(w_data), .en(e4), .clk(ck), .Q(r3), .clr(clear));
  Register #(.width(13)) register_14 (.D(w_data), .en(e8), .clk(ck), .Q(r7), .clr(clear));
  Register #(.width(13)) register_15 (.D(w_data), .en(e12), .clk(ck), .Q(r11), .clr(clear));
  Register #(.width(13)) register_16 (.D(w_data), .en(e16), .clk(ck), .Q(r15), .clr(clear));

  // Other names for the same wires on the sheet: c_reg[12:0] = r_data; r = clear; w_d[12:0] = w_data; w_E = WRITE;
  //   w_R = READ

  // Notes on the sheet:
  //   MUX
  //   ENTRADAS
  //   SAIDA
  //   DECODER
endmodule
